// Logisim project cpu24.circ as structural Verilog: 18 circuits, main circuit ◇单周期MIPS
module \单周期MIPS  (
  input  IR1,
  input  IR2,
  input  IR3,
  output RegWrite,
  output MemWrite,
  output [31:0] PC,
  output [31:0] IR,
  output [31:0] RDin,
  output [31:0] MDin,
  output [31:0] LedData
);

  wire and_1_out, and_3_out, and_4_out, and_5_out, CLK, clock_2_out, comparator_1_eq, comparator_2_eq,
       comparator_2_lt, comparator_3_gt, d_ff_1_q, Go, halt, IR1_t, IR2_t, IR3_t, IRA, IRB, IRC, LED,
       mips_alu_1_equal, nand_1_out, not_1_out, not_3_out, or_4_out, RST, SignedExt, Syscall, W1, W2, W3,
       \单周期硬布线控制器_1_alu_src , \单周期硬布线控制器_1_beq , \单周期硬布线控制器_1_bgtz , \单周期硬布线控制器_1_bne , \单周期硬布线控制器_1_jal ,
       \单周期硬布线控制器_1_jmp , \单周期硬布线控制器_1_jr , \单周期硬布线控制器_1_memtoreg , \单周期硬布线控制器_1_regdst , \单周期硬布线控制器_1_sh ;
  wire [3:0] mips_probe_1_p2;
  wire [4:0] multiplexer_4_out, multiplexer_5_out, multiplexer_6_out, multiplexer_7_out;
  wire [12:0] CNT_num;
  wire [15:0] \总周期数 ;
  wire [31:0] a0, bit_extender_1_out, bit_extender_2_out, JRPC, mips_alu_1_result, multiplexer_1_out,
       multiplexer_2_out, multiplexer_3_out, multiplexer_9_out, multiplexer_10_out, multiplexer_12_out,
       multiplexer_13_out, PC_4, ram_1_data, shifter_1_out, \条件跳转 ;

  Clock #(.highDuration(1), .lowDuration(1)) clock_1 ();  // open: out
  Button _1 (.out(IRA));
  Button _2 (.out(IRB));
  Button _3 (.out(IRC));
  Button \u_继续运行  (.out(Go));
  LED #(.active("true")) led_1 (.in(W1));
  LED #(.active("true")) led_2 (.in(W2));
  LED #(.active("true")) led_3 (.in(W3));
  Multiplexer #(.select(1), .width(32), .disabled("Z"), .enable("false")) multiplexer_1 (
    .in0(PC_4), .in1(\条件跳转 ), .out(multiplexer_1_out), .sel(or_4_out));
  Hex_Digit_Display hex_digit_display_1 (.value(LedData[31:28]));  // open: dp
  Multiplexer #(.select(1), .width(32), .disabled("Z"), .enable("false")) multiplexer_2 (
    .in0(multiplexer_1_out), .in1({PC_4[31:28], IR[25:0], 2'b00}), .out(multiplexer_2_out),
    .sel(\单周期硬布线控制器_1_jmp ));
  Hex_Digit_Display hex_digit_display_2 (.value(LedData[27:24]));  // open: dp
  Hex_Digit_Display hex_digit_display_3 (.value(LedData[23:20]));  // open: dp
  Multiplexer #(.select(1), .width(32), .disabled("Z"), .enable("false")) multiplexer_3 (
    .in0(multiplexer_2_out), .in1(JRPC), .out(multiplexer_3_out), .sel(\单周期硬布线控制器_1_jr ));
  Hex_Digit_Display hex_digit_display_4 (.value(LedData[15:12]));  // open: dp
  Hex_Digit_Display hex_digit_display_5 (.value(LedData[19:16]));  // open: dp
  Hex_Digit_Display hex_digit_display_6 (.value(LedData[11:8]));  // open: dp
  Hex_Digit_Display hex_digit_display_7 (.value(LedData[7:4]));  // open: dp
  // Probe on \总周期数 
  Comparator #(.width(32), .mode("twosComplement")) comparator_1 (
    .a(JRPC), .b(32'h32), .eq(comparator_1_eq));  // open: gt, lt
  Hex_Digit_Display hex_digit_display_8 (.value(LedData[3:0]));  // open: dp
  not not_1 (not_1_out, comparator_1_eq);
  and and_1 (and_1_out, Syscall, comparator_1_eq);
  not not_2 (halt, and_1_out);
  and and_2 (LED, Syscall, not_1_out);
  Register #(.width(32), .trigger("rising"), .Select("low")) u_PC (
    .D(multiplexer_3_out), .en(halt), .Q(PC), .clk(CLK), .clr(RST));
  D_Flip_Flop #(.trigger("high"), .Pre_Clr_Positions("LEGACY"), .NegatePresetClear("false"), .enable("true"), .NewFFLayout("false")) d_ff_1 (.Q(d_ff_1_q));  // open: clk, D, Qn, preset, en, reset
  or or_1 (IR1_t, IR1, IRA);
  Adder #(.width(32)) adder_1 (.a(PC), .b(32'h4), .out(PC_4));  // open: cin, cout
  // Probe on 13'h290
  or or_2 (IR2_t, IR2, IRB);
  Comparator #(.width(13), .mode("twosComplement")) comparator_2 (
    .a(CNT_num), .b(13'h290), .eq(comparator_2_eq), .lt(comparator_2_lt));  // open: gt
  Clock #(.highDuration(1), .lowDuration(1)) clock_2 (.out(clock_2_out));
  ROM #(.addrWidth(10), .dataWidth(32), .Select("high")) rom_1 (.addr(PC[11:2]), .data(IR));
  nand nand_1 (nand_1_out, d_ff_1_q, comparator_2_eq);
  Counter #(.width(13), .max('h1fff), .ongoal("stay"), .trigger("rising"), .behavior("old")) counter_1 (
    .count(comparator_2_lt), .Q(CNT_num), .clk(clock_2_out));  // open: load, D, carry, clr, preset
  or or_3 (IR3_t, IR3, IRC);
  // Mips_Probe mips_probe_1: pin names not known; wires that end beside it: IR, mips_probe_1_p2
  assign CLK = nand_1_out ? clock_2_out : 1'bz;  // Controlled_Buffer controlled_buffer_1
  Pull_Resistor #(.pull(1)) pull_resistor_1 (.node(CLK));
  \单周期硬布线控制器  \u_单周期硬布线控制器_1  (
    .Func(IR[5:0]), .OP(IR[31:26]), .ALU_OP(mips_probe_1_p2), .MemToReg(\单周期硬布线控制器_1_memtoreg ),
    .MemWrite(MemWrite), .ALU_SRC(\单周期硬布线控制器_1_alu_src ), .RegWrite(RegWrite), .SysCALL(Syscall),
    .SignedExt(SignedExt), .RegDst(\单周期硬布线控制器_1_regdst ), .JR(\单周期硬布线控制器_1_jr ), .JMP(\单周期硬布线控制器_1_jmp ),
    .Beq(\单周期硬布线控制器_1_beq ), .JAL(\单周期硬布线控制器_1_jal ), .Bne(\单周期硬布线控制器_1_bne ), .SH(\单周期硬布线控制器_1_sh ),
    .BGTZ(\单周期硬布线控制器_1_bgtz ));  // open: RtUsed, RsUsed, LUI
  Multiplexer #(.select(1), .width(5), .disabled("Z"), .enable("false")) multiplexer_4 (
    .in0(IR[20:16]), .in1(IR[15:11]), .out(multiplexer_4_out), .sel(\单周期硬布线控制器_1_regdst ));
  Multiplexer #(.select(1), .width(5), .disabled("Z"), .enable("false")) multiplexer_5 (
    .in0(IR[25:21]), .in1(5'b00010), .out(multiplexer_5_out), .sel(Syscall));
  Multiplexer #(.select(1), .width(5), .disabled("Z"), .enable("false")) multiplexer_6 (
    .in0(IR[20:16]), .in1(5'b00100), .out(multiplexer_6_out), .sel(Syscall));
  Multiplexer #(.select(1), .width(5), .disabled("Z"), .enable("false")) multiplexer_7 (
    .in0(multiplexer_4_out), .in1({5{1'b1}}), .out(multiplexer_7_out), .sel(\单周期硬布线控制器_1_jal ));
  Multiplexer #(.select(1), .width(32), .disabled("Z"), .enable("false")) multiplexer_8 (
    .in0(multiplexer_13_out), .in1(PC_4), .out(RDin), .sel(\单周期硬布线控制器_1_jal ));
  assign bit_extender_1_out = {{16{1'b0}}, IR[15:0]};  // Bit_Extender bit_extender_1
  assign bit_extender_2_out = {{16{IR[15]}}, IR[15:0]};  // Bit_Extender bit_extender_2
  Multiplexer #(.select(1), .width(32), .disabled("Z"), .enable("false")) multiplexer_9 (
    .in0(bit_extender_1_out), .in1(bit_extender_2_out), .out(multiplexer_9_out), .sel(SignedExt));
  MIPS_Regifile mips_regifile_1 (
    .Din(RDin), .Clk(CLK), .R1(JRPC), .R2(a0), .WE(RegWrite), .W_num(multiplexer_7_out),
    .R1_num(multiplexer_5_out), .R2_num(multiplexer_6_out));
  Comparator #(.width(32), .mode("twosComplement")) comparator_3 (
    .a(JRPC), .b({32{1'b0}}), .gt(comparator_3_gt));  // open: eq, lt
  Shifter #(.width(32), .shift("ll")) shifter_1 (.in(multiplexer_9_out), .\dist (5'b00010), .out(shifter_1_out));
  and and_3 (and_3_out, comparator_3_gt, \单周期硬布线控制器_1_bgtz );
  Multiplexer #(.select(1), .width(32), .disabled("Z"), .enable("false")) multiplexer_10 (
    .in0(a0), .in1(multiplexer_9_out), .out(multiplexer_10_out), .sel(\单周期硬布线控制器_1_alu_src ));
  Adder #(.width(32)) adder_2 (.a(shifter_1_out), .b(PC_4), .out(\条件跳转 ));  // open: cin, cout
  not not_3 (not_3_out, mips_alu_1_equal);
  MIPS_ALU mips_alu_1 (
    .X(JRPC), .Y(multiplexer_10_out), .AluOP(mips_probe_1_p2), .Equal(mips_alu_1_equal),
    .Result(mips_alu_1_result), .shamt(IR[10:6]));  // open: Result_2
  Register #(.width(32), .trigger("rising"), .Select("low")) register_1 (
    .D(a0), .en(LED), .Q(LedData), .clk(CLK));  // open: clr
  and and_4 (and_4_out, \单周期硬布线控制器_1_beq , mips_alu_1_equal);
  and and_5 (and_5_out, \单周期硬布线控制器_1_bne , not_3_out);
  Multiplexer #(.select(1), .width(32), .disabled("Z"), .enable("false")) multiplexer_11 (
    .in0(a0), .in1(multiplexer_12_out), .out(MDin), .sel(\单周期硬布线控制器_1_sh ));
  Multiplexer #(.select(1), .width(32), .disabled("Z"), .enable("false")) multiplexer_12 (
    .in0({ram_1_data[31:16], a0[15:0]}), .in1({a0[15:0], ram_1_data[15:0]}), .out(multiplexer_12_out),
    .sel(mips_alu_1_result[1]));
  or or_4 (or_4_out, and_4_out, and_3_out, and_5_out);
  Multiplexer #(.select(1), .width(32), .disabled("Z"), .enable("false")) multiplexer_13 (
    .in0(mips_alu_1_result), .in1(ram_1_data), .out(multiplexer_13_out), .sel(\单周期硬布线控制器_1_memtoreg ));
  RAM #(.addrWidth(10), .dataWidth(32), .bus("separate"), .Select("high")) ram_1 (
    .addr(mips_alu_1_result[11:2]), .din(MDin), .data(ram_1_data), .str(MemWrite), .clk(CLK));  // open: sel, ld, clr
  Button button_1 (.out(RST));
  Counter #(.width(16), .max('hffff), .ongoal("wrap"), .trigger("rising"), .behavior("new")) counter_2 (
    .count(halt), .Q(\总周期数 ), .clk(CLK), .clr(RST));  // open: load, D, carry, preset, down

  // Other names for the same wires on the sheet: v0[31:0] = JRPC; 无条件跳转[31:2] = {PC_4[31:28], IR[25:0]}

  // Notes on the sheet:
  //   中断源
  //   中断等待指示
  //   总复位信号应将除ROM以外所有存储组件全部清零
  //   数码管输出
  //   数码管输出应该用寄存器锁存，否则显示数据只能一闪而过
  //   戳工具置1进入计数暂停模式，ctrl+k时钟自动运行到对应节拍暂停
  //   ctrl+k关闭时钟连续运行，将控制位置零，进入单步调试模式调试
  //   用这个时钟源需要去掉电路中的其他时钟源
  //   控制位
  //   暂停节拍，不能为0
  //   指令存储器
  //   contents of rom_1 (hex, n*v repeats v):
  //   2008ffff 20090000 20111997 112020 20020022 c 2288820 2e291949 1120fffa 2002000a c
  //   OP
  //   Func
  //   rs
  //   指令字
  //   rt
  //   rd
  //   shamt
  //   imm
  //   可计数暂停的时钟源
  //   Func
  //   Beq
  //   JMP
  //   Bne
  //   JR
  //   JAL
  //   SH
  //   OP
  //   Syscall
  //   为方便自动评测，需要输出PC，IR，寄存器堆写如数据RDin
  //   MemToReg
  //   MemWrite
  //   AluOP
  //   AluSrcB
  //   RegWrite
  //   RegDst
  //   BGTZ
  //   RAM写使能MemWrite、RAM写入数据MDin等信号
endmodule

// 单周期硬布线控制器
module \单周期硬布线控制器  (
  input  [5:0] OP,
  input  [5:0] Func,
  output [3:0] ALU_OP,
  output MemToReg,
  output MemWrite,
  output ALU_SRC,
  output RegWrite,
  output LUI,
  output SysCALL,
  output RsUsed,
  output RtUsed,
  output SignedExt,
  output RegDst,
  output Beq,
  output Bne,
  output JR,
  output JMP,
  output JAL,
  output SH,
  output BGTZ
);

  \运算控制器自动生成  \u_运算控制器自动生成_1  (
    .OP0(OP[0]), .OP1(OP[1]), .OP2(OP[2]), .OP3(OP[3]), .OP4(OP[4]), .OP5(OP[5]), .F0(Func[0]), .F1(Func[1]),
    .F2(Func[2]), .F3(Func[3]), .F4(Func[4]), .F5(Func[5]), .S0(ALU_OP[0]), .S1(ALU_OP[1]), .S2(ALU_OP[2]),
    .S3(ALU_OP[3]));
  \控制信号自动生成  \u_控制信号自动生成_1  (
    .OP0(OP[0]), .OP1(OP[1]), .OP2(OP[2]), .OP3(OP[3]), .OP4(OP[4]), .OP5(OP[5]), .F0(Func[0]), .F1(Func[1]),
    .F2(Func[2]), .F3(Func[3]), .F4(Func[4]), .F5(Func[5]), .MemToReg(MemToReg), .MemWrite(MemWrite),
    .ALU_SRC(ALU_SRC), .RegWrite(RegWrite), .LUI(LUI), .SysCALL(SysCALL), .RsUsed(RsUsed), .RtUsed(RtUsed),
    .SignedExt(SignedExt), .RegDst(RegDst), .BEQ(Beq), .BNE(Bne), .JR(JR), .JUMP(JMP), .JAL(JAL), .SH(SH),
    .BGTZ(BGTZ));

  // Other names for the same wires on the sheet: OP_CODE[5:0] = OP

  // Notes on the sheet:
  //   运算器控制器，根据指令生成运算器功能选择信号
endmodule

// 运算器控制器
module \运算控制器自动生成  (
  input  OP0,
  input  OP1,
  input  OP2,
  input  OP3,
  input  OP4,
  input  OP5,
  input  F0,
  input  F1,
  input  F2,
  input  F3,
  input  F4,
  input  F5,
  output S0,
  output S1,
  output S2,
  output S3
);

  wire and_1_out, and_2_out, and_3_out, and_4_out, and_5_out, and_6_out, and_7_out, and_8_out, and_9_out,
       and_10_out, and_11_out, and_12_out, and_13_out, and_14_out, and_15_out, and_16_out, and_17_out,
       and_18_out, and_19_out, and_20_out, and_21_out, and_22_out, and_23_out, and_24_out, and_25_out,
       and_26_out, and_27_out, and_28_out, and_29_out, and_30_out, and_31_out, and_32_out, and_33_out,
       and_34_out, and_35_out, and_36_out, and_37_out, and_38_out, not_1_out, not_2_out, not_3_out,
       not_4_out, not_5_out, not_6_out, not_7_out, not_8_out, not_9_out, not_10_out, not_11_out, not_12_out,
       not_13_out, not_14_out, not_15_out, not_16_out, not_17_out, not_18_out, not_19_out, not_20_out,
       not_21_out, not_22_out, not_23_out, not_24_out, not_25_out, not_26_out, not_27_out, not_28_out,
       not_29_out, not_30_out, not_31_out, not_32_out, not_33_out, not_34_out, not_35_out, not_36_out,
       not_37_out, not_38_out, not_39_out, not_40_out, not_41_out, not_42_out, not_43_out, not_44_out,
       not_45_out, not_46_out, not_47_out, not_48_out, not_49_out, not_50_out, not_51_out, not_52_out,
       not_53_out, not_54_out, not_55_out, not_56_out, not_57_out, not_58_out, not_59_out, not_60_out,
       not_61_out, not_62_out, not_63_out, not_64_out, not_65_out, not_66_out, not_67_out, not_68_out,
       not_69_out, not_70_out, not_71_out, not_72_out, not_73_out, not_74_out, not_75_out, not_76_out,
       not_77_out, not_78_out, not_79_out, not_80_out, not_81_out, not_82_out, not_83_out, not_84_out,
       not_85_out, not_86_out, not_87_out, not_88_out, not_89_out, not_90_out, not_91_out, not_92_out,
       not_93_out, not_94_out, not_95_out, not_96_out, not_97_out, not_98_out, not_99_out, not_100_out,
       not_101_out, not_102_out, not_103_out, not_104_out, not_105_out, not_106_out, not_107_out,
       not_108_out, not_109_out, not_110_out, not_111_out, not_112_out, not_113_out, not_114_out,
       not_115_out, not_116_out, not_117_out, not_118_out, not_119_out, not_120_out, not_121_out,
       not_122_out, not_123_out, not_124_out, not_125_out, not_126_out, not_127_out, not_128_out,
       not_129_out, not_130_out, not_131_out, not_132_out, not_133_out, not_134_out, not_135_out,
       not_136_out, not_137_out, not_138_out, not_139_out, not_140_out, not_141_out, not_142_out,
       not_143_out, not_144_out, not_145_out, not_146_out, not_147_out, not_148_out, not_149_out,
       not_150_out, not_151_out, not_152_out, not_153_out, not_154_out, not_155_out, not_156_out,
       not_157_out, not_158_out, not_159_out, not_160_out, not_161_out, not_162_out, not_163_out,
       not_164_out, not_165_out, not_166_out, not_167_out, not_168_out, not_169_out, not_170_out,
       not_171_out, not_172_out, not_173_out, not_174_out, not_175_out, not_176_out, not_177_out,
       not_178_out, not_179_out, not_180_out, not_181_out, not_182_out, not_183_out, not_184_out,
       not_185_out, not_186_out, not_187_out, not_188_out, not_189_out, not_190_out, not_191_out,
       not_192_out, not_193_out, not_194_out, not_195_out, not_196_out, not_197_out, not_198_out,
       not_199_out, not_200_out, not_201_out, not_202_out, not_203_out, not_204_out, not_205_out,
       not_206_out, not_207_out, not_208_out, not_209_out, not_210_out, not_211_out, not_212_out,
       not_213_out, not_214_out, not_215_out, not_216_out, not_217_out, not_218_out, not_219_out,
       not_220_out, not_221_out, not_222_out, not_223_out, not_224_out, not_225_out, not_226_out,
       not_227_out, not_228_out, not_229_out, not_230_out, not_231_out, not_232_out, not_233_out,
       not_234_out, not_235_out, not_236_out, not_237_out, not_238_out, not_239_out, not_240_out,
       not_241_out, not_242_out, not_243_out, not_244_out, not_245_out, not_246_out, not_247_out, not_248_out;

  not not_1 (not_1_out, OP5);
  not not_2 (not_2_out, OP4);
  not not_3 (not_3_out, OP3);
  not not_4 (not_4_out, OP2);
  not not_5 (not_5_out, OP1);
  not not_6 (not_6_out, OP0);
  not not_7 (not_7_out, F5);
  not not_8 (not_8_out, F4);
  not not_9 (not_9_out, F3);
  not not_10 (not_10_out, F2);
  not not_11 (not_11_out, OP5);
  not not_12 (not_12_out, OP4);
  not not_13 (not_13_out, OP3);
  not not_14 (not_14_out, OP2);
  not not_15 (not_15_out, OP1);
  not not_16 (not_16_out, OP0);
  not not_17 (not_17_out, F4);
  not not_18 (not_18_out, F3);
  not not_19 (not_19_out, F2);
  not not_20 (not_20_out, F1);
  not not_21 (not_21_out, F0);
  not not_22 (not_22_out, OP5);
  not not_23 (not_23_out, OP4);
  not not_24 (not_24_out, OP3);
  not not_25 (not_25_out, OP2);
  not not_26 (not_26_out, OP1);
  not not_27 (not_27_out, OP0);
  not not_28 (not_28_out, F4);
  not not_29 (not_29_out, F3);
  not not_30 (not_30_out, F2);
  not not_31 (not_31_out, F1);
  not not_32 (not_32_out, OP5);
  not not_33 (not_33_out, OP4);
  not not_34 (not_34_out, OP3);
  not not_35 (not_35_out, OP2);
  not not_36 (not_36_out, OP1);
  not not_37 (not_37_out, OP0);
  not not_38 (not_38_out, F4);
  not not_39 (not_39_out, F3);
  not not_40 (not_40_out, F1);
  not not_41 (not_41_out, F0);
  not not_42 (not_42_out, OP5);
  not not_43 (not_43_out, OP4);
  not not_44 (not_44_out, OP3);
  not not_45 (not_45_out, OP2);
  not not_46 (not_46_out, OP1);
  not not_47 (not_47_out, OP0);
  not not_48 (not_48_out, F4);
  not not_49 (not_49_out, F2);
  not not_50 (not_50_out, F0);
  not not_51 (not_51_out, OP5);
  not not_52 (not_52_out, OP4);
  not not_53 (not_53_out, OP2);
  not not_54 (not_54_out, OP1);
  not not_55 (not_55_out, OP0);
  not not_56 (not_56_out, OP5);
  not not_57 (not_57_out, OP4);
  not not_58 (not_58_out, OP1);
  not not_59 (not_59_out, OP0);
  not not_60 (not_60_out, OP5);
  not not_61 (not_61_out, OP4);
  not not_62 (not_62_out, OP2);
  not not_63 (not_63_out, OP1);
  not not_64 (not_64_out, OP5);
  not not_65 (not_65_out, OP4);
  not not_66 (not_66_out, OP2);
  not not_67 (not_67_out, OP0);
  not not_68 (not_68_out, OP4);
  not not_69 (not_69_out, OP3);
  not not_70 (not_70_out, OP2);
  not not_71 (not_71_out, OP4);
  not not_72 (not_72_out, OP2);
  not not_73 (not_73_out, OP4);
  not not_74 (not_74_out, OP2);
  not not_75 (not_75_out, OP1);
  not not_76 (not_76_out, OP5);
  not not_77 (not_77_out, OP4);
  not not_78 (not_78_out, OP3);
  not not_79 (not_79_out, OP2);
  not not_80 (not_80_out, OP1);
  not not_81 (not_81_out, OP0);
  not not_82 (not_82_out, F5);
  not not_83 (not_83_out, F4);
  not not_84 (not_84_out, F3);
  not not_85 (not_85_out, F2);
  not not_86 (not_86_out, F0);
  not not_87 (not_87_out, OP5);
  not not_88 (not_88_out, OP4);
  not not_89 (not_89_out, OP3);
  not not_90 (not_90_out, OP2);
  not not_91 (not_91_out, OP1);
  not not_92 (not_92_out, OP0);
  not not_93 (not_93_out, F4);
  not not_94 (not_94_out, F3);
  not not_95 (not_95_out, F2);
  not not_96 (not_96_out, F0);
  not not_97 (not_97_out, OP5);
  not not_98 (not_98_out, OP4);
  not not_99 (not_99_out, OP3);
  not not_100 (not_100_out, OP2);
  not not_101 (not_101_out, OP1);
  not not_102 (not_102_out, OP0);
  not not_103 (not_103_out, F4);
  not not_104 (not_104_out, F3);
  not not_105 (not_105_out, F1);
  not not_106 (not_106_out, F0);
  not not_107 (not_107_out, OP5);
  not not_108 (not_108_out, OP4);
  not not_109 (not_109_out, OP3);
  not not_110 (not_110_out, OP2);
  not not_111 (not_111_out, OP1);
  not not_112 (not_112_out, OP0);
  not not_113 (not_113_out, F4);
  not not_114 (not_114_out, F3);
  not not_115 (not_115_out, OP5);
  not not_116 (not_116_out, OP4);
  not not_117 (not_117_out, OP3);
  not not_118 (not_118_out, OP2);
  not not_119 (not_119_out, OP1);
  not not_120 (not_120_out, OP0);
  not not_121 (not_121_out, F4);
  not not_122 (not_122_out, F2);
  not not_123 (not_123_out, F0);
  not not_124 (not_124_out, OP5);
  not not_125 (not_125_out, OP4);
  not not_126 (not_126_out, OP1);
  not not_127 (not_127_out, OP0);
  not not_128 (not_128_out, OP5);
  not not_129 (not_129_out, OP4);
  not not_130 (not_130_out, OP2);
  not not_131 (not_131_out, OP0);
  not not_132 (not_132_out, OP5);
  not not_133 (not_133_out, OP4);
  not not_134 (not_134_out, OP3);
  not not_135 (not_135_out, OP2);
  not not_136 (not_136_out, OP1);
  not not_137 (not_137_out, OP0);
  not not_138 (not_138_out, F4);
  not not_139 (not_139_out, F3);
  not not_140 (not_140_out, F2);
  not not_141 (not_141_out, F1);
  not not_142 (not_142_out, F0);
  not not_143 (not_143_out, OP5);
  not not_144 (not_144_out, OP4);
  not not_145 (not_145_out, OP3);
  not not_146 (not_146_out, OP2);
  not not_147 (not_147_out, OP1);
  not not_148 (not_148_out, OP0);
  not not_149 (not_149_out, F4);
  not not_150 (not_150_out, F3);
  not not_151 (not_151_out, F2);
  not not_152 (not_152_out, F1);
  not not_153 (not_153_out, OP5);
  not not_154 (not_154_out, OP4);
  not not_155 (not_155_out, OP3);
  not not_156 (not_156_out, OP2);
  not not_157 (not_157_out, OP1);
  not not_158 (not_158_out, OP0);
  not not_159 (not_159_out, F4);
  not not_160 (not_160_out, F3);
  not not_161 (not_161_out, F2);
  not not_162 (not_162_out, F0);
  not not_163 (not_163_out, OP5);
  not not_164 (not_164_out, OP4);
  not not_165 (not_165_out, OP3);
  not not_166 (not_166_out, OP2);
  not not_167 (not_167_out, OP1);
  not not_168 (not_168_out, OP0);
  not not_169 (not_169_out, F4);
  not not_170 (not_170_out, F3);
  not not_171 (not_171_out, F1);
  not not_172 (not_172_out, F0);
  not not_173 (not_173_out, OP5);
  not not_174 (not_174_out, OP4);
  not not_175 (not_175_out, OP3);
  not not_176 (not_176_out, OP2);
  not not_177 (not_177_out, OP1);
  not not_178 (not_178_out, OP0);
  not not_179 (not_179_out, F4);
  not not_180 (not_180_out, F2);
  not not_181 (not_181_out, OP5);
  not not_182 (not_182_out, OP4);
  not not_183 (not_183_out, OP2);
  not not_184 (not_184_out, OP1);
  not not_185 (not_185_out, OP0);
  not not_186 (not_186_out, OP5);
  not not_187 (not_187_out, OP4);
  not not_188 (not_188_out, OP1);
  not not_189 (not_189_out, OP0);
  not not_190 (not_190_out, OP5);
  not not_191 (not_191_out, OP4);
  not not_192 (not_192_out, OP2);
  not not_193 (not_193_out, OP1);
  not not_194 (not_194_out, OP4);
  not not_195 (not_195_out, OP3);
  not not_196 (not_196_out, OP2);
  not not_197 (not_197_out, OP4);
  not not_198 (not_198_out, OP2);
  not not_199 (not_199_out, OP5);
  not not_200 (not_200_out, OP4);
  not not_201 (not_201_out, OP2);
  not not_202 (not_202_out, OP4);
  not not_203 (not_203_out, OP2);
  not not_204 (not_204_out, OP1);
  not not_205 (not_205_out, OP5);
  not not_206 (not_206_out, OP4);
  not not_207 (not_207_out, OP3);
  not not_208 (not_208_out, OP2);
  not not_209 (not_209_out, OP1);
  not not_210 (not_210_out, OP0);
  not not_211 (not_211_out, F4);
  not not_212 (not_212_out, F3);
  not not_213 (not_213_out, F1);
  not not_214 (not_214_out, OP5);
  not not_215 (not_215_out, OP4);
  not not_216 (not_216_out, OP3);
  not not_217 (not_217_out, OP2);
  not not_218 (not_218_out, OP1);
  not not_219 (not_219_out, OP0);
  not not_220 (not_220_out, F4);
  not not_221 (not_221_out, F3);
  not not_222 (not_222_out, OP5);
  not not_223 (not_223_out, OP4);
  not not_224 (not_224_out, OP3);
  not not_225 (not_225_out, OP2);
  not not_226 (not_226_out, OP1);
  not not_227 (not_227_out, OP0);
  not not_228 (not_228_out, F4);
  not not_229 (not_229_out, F2);
  not not_230 (not_230_out, F0);
  not not_231 (not_231_out, OP5);
  not not_232 (not_232_out, OP4);
  not not_233 (not_233_out, OP3);
  not not_234 (not_234_out, OP2);
  not not_235 (not_235_out, OP1);
  not not_236 (not_236_out, OP0);
  not not_237 (not_237_out, F4);
  not not_238 (not_238_out, F2);
  not not_239 (not_239_out, OP5);
  not not_240 (not_240_out, OP4);
  not not_241 (not_241_out, OP2);
  not not_242 (not_242_out, OP0);
  not not_243 (not_243_out, OP5);
  not not_244 (not_244_out, OP4);
  not not_245 (not_245_out, OP1);
  not not_246 (not_246_out, OP5);
  not not_247 (not_247_out, OP4);
  not not_248 (not_248_out, OP2);
  and and_1 (and_1_out, not_1_out, not_2_out, not_3_out, not_4_out, not_5_out, not_6_out, not_7_out, not_8_out, not_9_out, not_10_out, F1, F0);
  and and_2 (and_2_out, not_11_out, not_12_out, not_13_out, not_14_out, not_15_out, not_16_out, F5, not_17_out, not_18_out, not_19_out, not_20_out, not_21_out);
  and and_3 (and_3_out, not_22_out, not_23_out, not_24_out, not_25_out, not_26_out, not_27_out, F5, not_28_out, not_29_out, not_30_out, not_31_out, F0);
  and and_4 (and_4_out, not_32_out, not_33_out, not_34_out, not_35_out, not_36_out, not_37_out, F5, not_38_out, not_39_out, F2, not_40_out, not_41_out);
  and and_5 (and_5_out, not_42_out, not_43_out, not_44_out, not_45_out, not_46_out, not_47_out, F5, not_48_out, F3, not_49_out, F1, not_50_out);
  and and_6 (and_6_out, not_51_out, not_52_out, OP3, not_53_out, not_54_out, not_55_out);
  and and_7 (and_7_out, not_56_out, not_57_out, OP3, OP2, not_58_out, not_59_out);
  and and_8 (and_8_out, not_60_out, not_61_out, OP3, not_62_out, not_63_out, OP0);
  and and_9 (and_9_out, not_64_out, not_65_out, OP3, not_66_out, OP1, not_67_out);
  and and_10 (and_10_out, OP5, not_68_out, not_69_out, not_70_out, OP1, OP0);
  and and_11 (and_11_out, OP5, not_71_out, OP3, not_72_out, OP1, OP0);
  and and_12 (and_12_out, OP5, not_73_out, OP3, not_74_out, not_75_out, OP0);
  and and_13 (and_13_out, not_76_out, not_77_out, not_78_out, not_79_out, not_80_out, not_81_out, not_82_out, not_83_out, not_84_out, not_85_out, F1, not_86_out);
  and and_14 (and_14_out, not_87_out, not_88_out, not_89_out, not_90_out, not_91_out, not_92_out, F5, not_93_out, not_94_out, not_95_out, F1, not_96_out);
  and and_15 (and_15_out, not_97_out, not_98_out, not_99_out, not_100_out, not_101_out, not_102_out, F5, not_103_out, not_104_out, F2, not_105_out, not_106_out);
  and and_16 (and_16_out, not_107_out, not_108_out, not_109_out, not_110_out, not_111_out, not_112_out, F5, not_113_out, not_114_out, F2, F1, F0);
  and and_17 (and_17_out, not_115_out, not_116_out, not_117_out, not_118_out, not_119_out, not_120_out, F5, not_121_out, F3, not_122_out, F1, not_123_out);
  and and_18 (and_18_out, not_124_out, not_125_out, OP3, OP2, not_126_out, not_127_out);
  and and_19 (and_19_out, not_128_out, not_129_out, OP3, not_130_out, OP1, not_131_out);
  and and_20 (and_20_out, not_132_out, not_133_out, not_134_out, not_135_out, not_136_out, not_137_out, F5, not_138_out, not_139_out, not_140_out, not_141_out, not_142_out);
  and and_21 (and_21_out, not_143_out, not_144_out, not_145_out, not_146_out, not_147_out, not_148_out, F5, not_149_out, not_150_out, not_151_out, not_152_out, F0);
  and and_22 (and_22_out, not_153_out, not_154_out, not_155_out, not_156_out, not_157_out, not_158_out, F5, not_159_out, not_160_out, not_161_out, F1, not_162_out);
  and and_23 (and_23_out, not_163_out, not_164_out, not_165_out, not_166_out, not_167_out, not_168_out, F5, not_169_out, not_170_out, F2, not_171_out, not_172_out);
  and and_24 (and_24_out, not_173_out, not_174_out, not_175_out, not_176_out, not_177_out, not_178_out, F5, not_179_out, F3, not_180_out, F1, F0);
  and and_25 (and_25_out, not_181_out, not_182_out, OP3, not_183_out, not_184_out, not_185_out);
  and and_26 (and_26_out, not_186_out, not_187_out, OP3, OP2, not_188_out, not_189_out);
  and and_27 (and_27_out, not_190_out, not_191_out, OP3, not_192_out, not_193_out, OP0);
  and and_28 (and_28_out, OP5, not_194_out, not_195_out, not_196_out, OP1, OP0);
  and and_29 (and_29_out, OP5, not_197_out, OP3, not_198_out, OP1, OP0);
  and and_30 (and_30_out, not_199_out, not_200_out, OP3, not_201_out, OP1, OP0);
  and and_31 (and_31_out, OP5, not_202_out, OP3, not_203_out, not_204_out, OP0);
  and and_32 (and_32_out, not_205_out, not_206_out, not_207_out, not_208_out, not_209_out, not_210_out, F5, not_211_out, not_212_out, F2, not_213_out, F0);
  and and_33 (and_33_out, not_214_out, not_215_out, not_216_out, not_217_out, not_218_out, not_219_out, F5, not_220_out, not_221_out, F2, F1, F0);
  and and_34 (and_34_out, not_222_out, not_223_out, not_224_out, not_225_out, not_226_out, not_227_out, F5, not_228_out, F3, not_229_out, F1, not_230_out);
  and and_35 (and_35_out, not_231_out, not_232_out, not_233_out, not_234_out, not_235_out, not_236_out, F5, not_237_out, F3, not_238_out, F1, F0);
  and and_36 (and_36_out, not_239_out, not_240_out, OP3, not_241_out, OP1, not_242_out);
  and and_37 (and_37_out, not_243_out, not_244_out, OP3, OP2, not_245_out, OP0);
  and and_38 (and_38_out, not_246_out, not_247_out, OP3, not_248_out, OP1, OP0);
  or or_1 (S1, and_13_out, and_14_out, and_15_out, and_16_out, and_17_out, and_18_out, and_19_out);
  or or_2 (S3, and_32_out, and_33_out, and_34_out, and_35_out, and_36_out, and_37_out, and_38_out);
  or or_3 (S0, and_1_out, and_2_out, and_3_out, and_4_out, and_5_out, and_6_out, and_7_out, and_8_out, and_9_out, and_10_out, and_11_out, and_12_out);
  or or_4 (S2, and_20_out, and_21_out, and_22_out, and_23_out, and_24_out, and_25_out, and_26_out, and_27_out, and_28_out, and_29_out, and_30_out, and_31_out);
endmodule

// 控制信号生成
module \控制信号自动生成  (
  input  OP0,
  input  OP1,
  input  OP2,
  input  OP3,
  input  OP4,
  input  OP5,
  input  F0,
  input  F1,
  input  F2,
  input  F3,
  input  F4,
  input  F5,
  output MemToReg,
  output MemWrite,
  output ALU_SRC,
  output RegWrite,
  output LUI,
  output SysCALL,
  output RsUsed,
  output RtUsed,
  output SignedExt,
  output RegDst,
  output BEQ,
  output BNE,
  output JR,
  output JUMP,
  output JAL,
  output SH,
  output BGTZ
);

  wire and_2_out, and_3_out, and_4_out, and_5_out, and_6_out, and_7_out, and_8_out, and_9_out, and_10_out,
       and_11_out, and_12_out, and_13_out, and_14_out, and_15_out, and_16_out, and_17_out, and_18_out,
       and_19_out, and_20_out, and_21_out, and_22_out, and_23_out, and_24_out, and_25_out, and_26_out,
       and_27_out, and_28_out, and_29_out, and_30_out, and_31_out, and_32_out, and_33_out, and_36_out,
       and_37_out, and_38_out, and_39_out, and_40_out, and_41_out, and_42_out, and_43_out, and_44_out,
       and_45_out, and_46_out, and_47_out, and_48_out, and_49_out, and_50_out, and_51_out, and_52_out,
       and_53_out, and_54_out, and_55_out, and_56_out, and_57_out, and_58_out, and_59_out, and_60_out,
       and_61_out, and_62_out, and_63_out, and_64_out, and_65_out, and_66_out, and_67_out, and_68_out,
       and_69_out, and_70_out, and_71_out, and_72_out, and_73_out, and_74_out, and_78_out, and_79_out,
       and_80_out, not_1_out, not_2_out, not_3_out, not_4_out, not_5_out, not_6_out, not_7_out, not_8_out,
       not_9_out, not_10_out, not_11_out, not_12_out, not_13_out, not_14_out, not_15_out, not_16_out,
       not_17_out, not_18_out, not_19_out, not_20_out, not_21_out, not_22_out, not_23_out, not_24_out,
       not_25_out, not_26_out, not_27_out, not_28_out, not_29_out, not_30_out, not_31_out, not_32_out,
       not_33_out, not_34_out, not_35_out, not_36_out, not_37_out, not_38_out, not_39_out, not_40_out,
       not_41_out, not_42_out, not_43_out, not_44_out, not_45_out, not_46_out, not_47_out, not_48_out,
       not_49_out, not_50_out, not_51_out, not_52_out, not_53_out, not_54_out, not_55_out, not_56_out,
       not_57_out, not_58_out, not_59_out, not_60_out, not_61_out, not_62_out, not_63_out, not_64_out,
       not_65_out, not_66_out, not_67_out, not_68_out, not_69_out, not_70_out, not_71_out, not_72_out,
       not_73_out, not_74_out, not_75_out, not_76_out, not_77_out, not_78_out, not_79_out, not_80_out,
       not_81_out, not_82_out, not_83_out, not_84_out, not_85_out, not_86_out, not_87_out, not_88_out,
       not_89_out, not_90_out, not_91_out, not_92_out, not_93_out, not_94_out, not_95_out, not_96_out,
       not_97_out, not_98_out, not_99_out, not_100_out, not_101_out, not_102_out, not_103_out, not_104_out,
       not_105_out, not_106_out, not_107_out, not_108_out, not_109_out, not_110_out, not_111_out,
       not_112_out, not_113_out, not_114_out, not_115_out, not_116_out, not_117_out, not_118_out,
       not_119_out, not_120_out, not_121_out, not_122_out, not_123_out, not_124_out, not_125_out,
       not_126_out, not_127_out, not_128_out, not_129_out, not_130_out, not_131_out, not_132_out,
       not_133_out, not_134_out, not_135_out, not_136_out, not_137_out, not_138_out, not_139_out,
       not_140_out, not_141_out, not_142_out, not_143_out, not_144_out, not_145_out, not_146_out,
       not_147_out, not_148_out, not_149_out, not_150_out, not_151_out, not_152_out, not_153_out,
       not_154_out, not_155_out, not_156_out, not_157_out, not_158_out, not_159_out, not_160_out,
       not_161_out, not_162_out, not_163_out, not_164_out, not_165_out, not_166_out, not_167_out,
       not_168_out, not_169_out, not_170_out, not_171_out, not_172_out, not_173_out, not_174_out,
       not_175_out, not_176_out, not_177_out, not_178_out, not_179_out, not_180_out, not_181_out,
       not_182_out, not_183_out, not_184_out, not_185_out, not_186_out, not_187_out, not_188_out,
       not_189_out, not_190_out, not_191_out, not_192_out, not_193_out, not_194_out, not_195_out,
       not_196_out, not_197_out, not_198_out, not_199_out, not_200_out, not_201_out, not_202_out,
       not_203_out, not_204_out, not_205_out, not_206_out, not_207_out, not_208_out, not_209_out,
       not_210_out, not_211_out, not_212_out, not_213_out, not_214_out, not_215_out, not_216_out,
       not_217_out, not_218_out, not_219_out, not_220_out, not_221_out, not_222_out, not_223_out,
       not_224_out, not_225_out, not_226_out, not_227_out, not_228_out, not_229_out, not_230_out,
       not_231_out, not_232_out, not_233_out, not_234_out, not_235_out, not_236_out, not_237_out,
       not_238_out, not_239_out, not_240_out, not_241_out, not_242_out, not_243_out, not_244_out,
       not_245_out, not_246_out, not_247_out, not_248_out, not_249_out, not_250_out, not_251_out,
       not_252_out, not_253_out, not_254_out, not_255_out, not_256_out, not_257_out, not_258_out,
       not_259_out, not_260_out, not_261_out, not_262_out, not_263_out, not_264_out, not_265_out,
       not_266_out, not_267_out, not_268_out, not_269_out, not_270_out, not_271_out, not_272_out,
       not_273_out, not_274_out, not_275_out, not_276_out, not_277_out, not_278_out, not_279_out,
       not_280_out, not_281_out, not_282_out, not_283_out, not_284_out, not_285_out, not_286_out,
       not_287_out, not_288_out, not_289_out, not_290_out, not_291_out, not_292_out, not_293_out,
       not_294_out, not_295_out, not_296_out, not_297_out, not_298_out, not_299_out, not_300_out,
       not_301_out, not_302_out, not_303_out, not_304_out, not_305_out, not_306_out, not_307_out,
       not_308_out, not_309_out, not_310_out, not_311_out, not_312_out, not_313_out, not_314_out,
       not_315_out, not_316_out, not_317_out, not_318_out, not_319_out, not_320_out, not_321_out,
       not_322_out, not_323_out, not_324_out, not_325_out, not_326_out, not_327_out, not_328_out,
       not_329_out, not_330_out, not_331_out, not_332_out, not_333_out, not_334_out, not_335_out,
       not_336_out, not_337_out, not_338_out, not_339_out, not_340_out, not_341_out, not_342_out,
       not_343_out, not_344_out, not_345_out, not_346_out, not_347_out, not_348_out, not_349_out,
       not_350_out, not_351_out, not_352_out, not_353_out, not_354_out, not_355_out, not_356_out,
       not_357_out, not_358_out, not_359_out, not_360_out, not_361_out, not_362_out, not_363_out,
       not_364_out, not_365_out, not_366_out, not_367_out, not_368_out, not_369_out, not_370_out,
       not_371_out, not_372_out, not_373_out, not_374_out, not_375_out, not_376_out, not_377_out,
       not_378_out, not_379_out, not_380_out, not_381_out, not_382_out, not_383_out, not_384_out,
       not_385_out, not_386_out, not_387_out, not_388_out, not_389_out, not_390_out, not_391_out,
       not_392_out, not_393_out, not_394_out, not_395_out, not_396_out, not_397_out, not_398_out,
       not_399_out, not_400_out, not_401_out, not_402_out, not_403_out, not_404_out, not_405_out,
       not_406_out, not_407_out, not_408_out, not_409_out, not_410_out, not_411_out, not_412_out,
       not_413_out, not_414_out, not_415_out, not_416_out, not_417_out, not_418_out, not_419_out,
       not_420_out, not_421_out, not_422_out, not_423_out, not_424_out, not_425_out, not_426_out,
       not_427_out, not_428_out, not_429_out, not_430_out, not_431_out, not_432_out, not_433_out,
       not_434_out, not_435_out, not_436_out, not_437_out, not_438_out, not_439_out, not_440_out,
       not_441_out, not_442_out, not_443_out, not_444_out, not_445_out, not_446_out, not_447_out,
       not_448_out, not_449_out, not_450_out, not_451_out, not_452_out, not_453_out, not_454_out,
       not_455_out, not_456_out, not_457_out, not_458_out, not_459_out, not_460_out, not_461_out,
       not_462_out, not_463_out, not_464_out, not_465_out, not_466_out, not_467_out, not_468_out,
       not_469_out, not_470_out, not_471_out, not_472_out, not_473_out, not_474_out, not_475_out,
       not_476_out, not_477_out, not_478_out, not_479_out, not_480_out, not_481_out, not_482_out,
       not_483_out, not_484_out, not_485_out, not_486_out, not_487_out, not_488_out, not_489_out,
       not_490_out, not_491_out, not_492_out, not_493_out, not_494_out, not_495_out, not_496_out,
       not_497_out, not_498_out;

  not not_1 (not_1_out, OP4);
  not not_2 (not_2_out, OP3);
  not not_3 (not_3_out, OP2);
  not not_4 (not_4_out, OP4);
  not not_5 (not_5_out, OP2);
  not not_6 (not_6_out, OP4);
  not not_7 (not_7_out, OP2);
  not not_8 (not_8_out, OP1);
  not not_9 (not_9_out, OP5);
  not not_10 (not_10_out, OP4);
  not not_11 (not_11_out, OP2);
  not not_12 (not_12_out, OP1);
  not not_13 (not_13_out, OP0);
  not not_14 (not_14_out, OP5);
  not not_15 (not_15_out, OP4);
  not not_16 (not_16_out, OP1);
  not not_17 (not_17_out, OP0);
  not not_18 (not_18_out, OP5);
  not not_19 (not_19_out, OP4);
  not not_20 (not_20_out, OP2);
  not not_21 (not_21_out, OP1);
  not not_22 (not_22_out, OP5);
  not not_23 (not_23_out, OP4);
  not not_24 (not_24_out, OP2);
  not not_25 (not_25_out, OP0);
  not not_26 (not_26_out, OP5);
  not not_27 (not_27_out, OP4);
  not not_28 (not_28_out, OP1);
  not not_29 (not_29_out, OP4);
  not not_30 (not_30_out, OP3);
  not not_31 (not_31_out, OP2);
  not not_32 (not_32_out, OP4);
  not not_33 (not_33_out, OP2);
  not not_34 (not_34_out, OP5);
  not not_35 (not_35_out, OP4);
  not not_36 (not_36_out, OP5);
  not not_37 (not_37_out, OP4);
  not not_38 (not_38_out, OP2);
  not not_39 (not_39_out, OP4);
  not not_40 (not_40_out, OP2);
  not not_41 (not_41_out, OP1);
  not not_42 (not_42_out, OP5);
  not not_43 (not_43_out, OP4);
  not not_44 (not_44_out, OP3);
  not not_45 (not_45_out, OP2);
  not not_46 (not_46_out, OP1);
  not not_47 (not_47_out, OP0);
  not not_48 (not_48_out, F5);
  not not_49 (not_49_out, F4);
  not not_50 (not_50_out, F3);
  not not_51 (not_51_out, F2);
  not not_52 (not_52_out, F1);
  not not_53 (not_53_out, F0);
  not not_54 (not_54_out, OP5);
  not not_55 (not_55_out, OP4);
  not not_56 (not_56_out, OP3);
  not not_57 (not_57_out, OP2);
  not not_58 (not_58_out, OP1);
  not not_59 (not_59_out, OP0);
  not not_60 (not_60_out, F5);
  not not_61 (not_61_out, F4);
  not not_62 (not_62_out, F3);
  not not_63 (not_63_out, F2);
  not not_64 (not_64_out, OP5);
  not not_65 (not_65_out, OP4);
  not not_66 (not_66_out, OP3);
  not not_67 (not_67_out, OP2);
  not not_68 (not_68_out, OP1);
  not not_69 (not_69_out, OP0);
  not not_70 (not_70_out, F5);
  not not_71 (not_71_out, F4);
  not not_72 (not_72_out, F3);
  not not_73 (not_73_out, F2);
  not not_74 (not_74_out, F0);
  not not_75 (not_75_out, OP5);
  not not_76 (not_76_out, OP4);
  not not_77 (not_77_out, OP3);
  not not_78 (not_78_out, OP2);
  not not_79 (not_79_out, OP1);
  not not_80 (not_80_out, OP0);
  not not_81 (not_81_out, F4);
  not not_82 (not_82_out, F3);
  not not_83 (not_83_out, F2);
  not not_84 (not_84_out, F1);
  not not_85 (not_85_out, F0);
  not not_86 (not_86_out, OP5);
  not not_87 (not_87_out, OP4);
  not not_88 (not_88_out, OP3);
  not not_89 (not_89_out, OP2);
  not not_90 (not_90_out, OP1);
  not not_91 (not_91_out, OP0);
  not not_92 (not_92_out, F4);
  not not_93 (not_93_out, F3);
  not not_94 (not_94_out, F2);
  not not_95 (not_95_out, F1);
  not not_96 (not_96_out, OP5);
  not not_97 (not_97_out, OP4);
  not not_98 (not_98_out, OP3);
  not not_99 (not_99_out, OP2);
  not not_100 (not_100_out, OP1);
  not not_101 (not_101_out, OP0);
  not not_102 (not_102_out, F4);
  not not_103 (not_103_out, F3);
  not not_104 (not_104_out, F2);
  not not_105 (not_105_out, F0);
  not not_106 (not_106_out, OP5);
  not not_107 (not_107_out, OP4);
  not not_108 (not_108_out, OP3);
  not not_109 (not_109_out, OP2);
  not not_110 (not_110_out, OP1);
  not not_111 (not_111_out, OP0);
  not not_112 (not_112_out, F4);
  not not_113 (not_113_out, F3);
  not not_114 (not_114_out, F1);
  not not_115 (not_115_out, F0);
  not not_116 (not_116_out, OP5);
  not not_117 (not_117_out, OP4);
  not not_118 (not_118_out, OP3);
  not not_119 (not_119_out, OP2);
  not not_120 (not_120_out, OP1);
  not not_121 (not_121_out, OP0);
  not not_122 (not_122_out, F4);
  not not_123 (not_123_out, F3);
  not not_124 (not_124_out, F1);
  not not_125 (not_125_out, OP5);
  not not_126 (not_126_out, OP4);
  not not_127 (not_127_out, OP3);
  not not_128 (not_128_out, OP2);
  not not_129 (not_129_out, OP1);
  not not_130 (not_130_out, OP0);
  not not_131 (not_131_out, F4);
  not not_132 (not_132_out, F3);
  not not_133 (not_133_out, OP5);
  not not_134 (not_134_out, OP4);
  not not_135 (not_135_out, OP3);
  not not_136 (not_136_out, OP2);
  not not_137 (not_137_out, OP1);
  not not_138 (not_138_out, OP0);
  not not_139 (not_139_out, F4);
  not not_140 (not_140_out, F2);
  not not_141 (not_141_out, F0);
  not not_142 (not_142_out, OP5);
  not not_143 (not_143_out, OP4);
  not not_144 (not_144_out, OP3);
  not not_145 (not_145_out, OP2);
  not not_146 (not_146_out, OP1);
  not not_147 (not_147_out, OP0);
  not not_148 (not_148_out, F4);
  not not_149 (not_149_out, F2);
  not not_150 (not_150_out, OP5);
  not not_151 (not_151_out, OP4);
  not not_152 (not_152_out, OP3);
  not not_153 (not_153_out, OP2);
  not not_154 (not_154_out, OP5);
  not not_155 (not_155_out, OP4);
  not not_156 (not_156_out, OP2);
  not not_157 (not_157_out, OP1);
  not not_158 (not_158_out, OP0);
  not not_159 (not_159_out, OP5);
  not not_160 (not_160_out, OP4);
  not not_161 (not_161_out, OP1);
  not not_162 (not_162_out, OP0);
  not not_163 (not_163_out, OP5);
  not not_164 (not_164_out, OP4);
  not not_165 (not_165_out, OP2);
  not not_166 (not_166_out, OP1);
  not not_167 (not_167_out, OP5);
  not not_168 (not_168_out, OP4);
  not not_169 (not_169_out, OP2);
  not not_170 (not_170_out, OP0);
  not not_171 (not_171_out, OP5);
  not not_172 (not_172_out, OP4);
  not not_173 (not_173_out, OP1);
  not not_174 (not_174_out, OP4);
  not not_175 (not_175_out, OP3);
  not not_176 (not_176_out, OP2);
  not not_177 (not_177_out, OP5);
  not not_178 (not_178_out, OP4);
  not not_179 (not_179_out, OP5);
  not not_180 (not_180_out, OP4);
  not not_181 (not_181_out, OP2);
  not not_182 (not_182_out, OP5);
  not not_183 (not_183_out, OP4);
  not not_184 (not_184_out, OP5);
  not not_185 (not_185_out, OP4);
  not not_186 (not_186_out, OP3);
  not not_187 (not_187_out, OP2);
  not not_188 (not_188_out, OP1);
  not not_189 (not_189_out, OP0);
  not not_190 (not_190_out, F5);
  not not_191 (not_191_out, F4);
  not not_192 (not_192_out, F1);
  not not_193 (not_193_out, F0);
  not not_194 (not_194_out, OP0);
  not not_195 (not_195_out, OP1);
  not not_196 (not_196_out, OP4);
  not not_197 (not_197_out, OP5);
  not not_198 (not_198_out, F0);
  not not_199 (not_199_out, F2);
  not not_200 (not_200_out, F3);
  not not_201 (not_201_out, F4);
  not not_202 (not_202_out, OP0);
  not not_203 (not_203_out, OP1);
  not not_204 (not_204_out, OP4);
  not not_205 (not_205_out, OP5);
  not not_206 (not_206_out, F3);
  not not_207 (not_207_out, F4);
  not not_208 (not_208_out, OP0);
  not not_209 (not_209_out, OP1);
  not not_210 (not_210_out, OP4);
  not not_211 (not_211_out, OP5);
  not not_212 (not_212_out, F0);
  not not_213 (not_213_out, F1);
  not not_214 (not_214_out, F4);
  not not_215 (not_215_out, F5);
  not not_216 (not_216_out, OP0);
  not not_217 (not_217_out, OP1);
  not not_218 (not_218_out, OP4);
  not not_219 (not_219_out, OP5);
  not not_220 (not_220_out, F2);
  not not_221 (not_221_out, F3);
  not not_222 (not_222_out, F4);
  not not_223 (not_223_out, OP0);
  not not_224 (not_224_out, OP1);
  not not_225 (not_225_out, OP4);
  not not_226 (not_226_out, OP5);
  not not_227 (not_227_out, F2);
  not not_228 (not_228_out, F4);
  not not_229 (not_229_out, OP0);
  not not_230 (not_230_out, OP1);
  not not_231 (not_231_out, OP2);
  not not_232 (not_232_out, OP4);
  not not_233 (not_233_out, OP0);
  not not_234 (not_234_out, OP2);
  not not_235 (not_235_out, OP4);
  not not_236 (not_236_out, OP5);
  not not_237 (not_237_out, OP1);
  not not_238 (not_238_out, OP4);
  not not_239 (not_239_out, OP5);
  not not_240 (not_240_out, OP0);
  not not_241 (not_241_out, OP3);
  not not_242 (not_242_out, OP4);
  not not_243 (not_243_out, OP5);
  not not_244 (not_244_out, OP1);
  not not_245 (not_245_out, OP4);
  not not_246 (not_246_out, OP5);
  not not_247 (not_247_out, OP2);
  not not_248 (not_248_out, OP4);
  not not_249 (not_249_out, OP0);
  not not_250 (not_250_out, OP1);
  not not_251 (not_251_out, OP3);
  not not_252 (not_252_out, OP4);
  not not_253 (not_253_out, OP5);
  not not_254 (not_254_out, F0);
  not not_255 (not_255_out, F2);
  not not_256 (not_256_out, F3);
  not not_257 (not_257_out, F4);
  not not_258 (not_258_out, OP0);
  not not_259 (not_259_out, OP1);
  not not_260 (not_260_out, OP3);
  not not_261 (not_261_out, OP4);
  not not_262 (not_262_out, OP5);
  not not_263 (not_263_out, F1);
  not not_264 (not_264_out, F3);
  not not_265 (not_265_out, F4);
  not not_266 (not_266_out, OP0);
  not not_267 (not_267_out, OP1);
  not not_268 (not_268_out, OP3);
  not not_269 (not_269_out, OP4);
  not not_270 (not_270_out, OP5);
  not not_271 (not_271_out, F0);
  not not_272 (not_272_out, F1);
  not not_273 (not_273_out, F4);
  not not_274 (not_274_out, F5);
  not not_275 (not_275_out, OP0);
  not not_276 (not_276_out, OP1);
  not not_277 (not_277_out, OP3);
  not not_278 (not_278_out, OP4);
  not not_279 (not_279_out, OP5);
  not not_280 (not_280_out, F2);
  not not_281 (not_281_out, F3);
  not not_282 (not_282_out, F4);
  not not_283 (not_283_out, F5);
  not not_284 (not_284_out, OP0);
  not not_285 (not_285_out, OP1);
  not not_286 (not_286_out, OP3);
  not not_287 (not_287_out, OP4);
  not not_288 (not_288_out, OP5);
  not not_289 (not_289_out, F2);
  not not_290 (not_290_out, F4);
  not not_291 (not_291_out, OP0);
  not not_292 (not_292_out, OP1);
  not not_293 (not_293_out, OP3);
  not not_294 (not_294_out, OP4);
  not not_295 (not_295_out, OP5);
  not not_296 (not_296_out, F3);
  not not_297 (not_297_out, F4);
  not not_298 (not_298_out, OP1);
  not not_299 (not_299_out, OP3);
  not not_300 (not_300_out, OP4);
  not not_301 (not_301_out, OP5);
  not not_302 (not_302_out, OP2);
  not not_303 (not_303_out, OP4);
  not not_304 (not_304_out, OP4);
  not not_305 (not_305_out, OP5);
  not not_306 (not_306_out, OP5);
  not not_307 (not_307_out, OP4);
  not not_308 (not_308_out, OP2);
  not not_309 (not_309_out, OP1);
  not not_310 (not_310_out, OP0);
  not not_311 (not_311_out, OP5);
  not not_312 (not_312_out, OP4);
  not not_313 (not_313_out, OP2);
  not not_314 (not_314_out, OP1);
  not not_315 (not_315_out, OP5);
  not not_316 (not_316_out, OP4);
  not not_317 (not_317_out, OP2);
  not not_318 (not_318_out, OP0);
  not not_319 (not_319_out, OP4);
  not not_320 (not_320_out, OP3);
  not not_321 (not_321_out, OP2);
  not not_322 (not_322_out, OP4);
  not not_323 (not_323_out, OP2);
  not not_324 (not_324_out, OP5);
  not not_325 (not_325_out, OP4);
  not not_326 (not_326_out, OP2);
  not not_327 (not_327_out, OP4);
  not not_328 (not_328_out, OP2);
  not not_329 (not_329_out, OP1);
  not not_330 (not_330_out, OP5);
  not not_331 (not_331_out, OP4);
  not not_332 (not_332_out, OP3);
  not not_333 (not_333_out, OP2);
  not not_334 (not_334_out, OP1);
  not not_335 (not_335_out, OP0);
  not not_336 (not_336_out, F5);
  not not_337 (not_337_out, F4);
  not not_338 (not_338_out, F3);
  not not_339 (not_339_out, F2);
  not not_340 (not_340_out, F1);
  not not_341 (not_341_out, F0);
  not not_342 (not_342_out, OP5);
  not not_343 (not_343_out, OP4);
  not not_344 (not_344_out, OP3);
  not not_345 (not_345_out, OP2);
  not not_346 (not_346_out, OP1);
  not not_347 (not_347_out, OP0);
  not not_348 (not_348_out, F5);
  not not_349 (not_349_out, F4);
  not not_350 (not_350_out, F3);
  not not_351 (not_351_out, F2);
  not not_352 (not_352_out, OP5);
  not not_353 (not_353_out, OP4);
  not not_354 (not_354_out, OP3);
  not not_355 (not_355_out, OP2);
  not not_356 (not_356_out, OP1);
  not not_357 (not_357_out, OP0);
  not not_358 (not_358_out, F5);
  not not_359 (not_359_out, F4);
  not not_360 (not_360_out, F3);
  not not_361 (not_361_out, F2);
  not not_362 (not_362_out, F0);
  not not_363 (not_363_out, OP5);
  not not_364 (not_364_out, OP4);
  not not_365 (not_365_out, OP3);
  not not_366 (not_366_out, OP2);
  not not_367 (not_367_out, OP1);
  not not_368 (not_368_out, OP0);
  not not_369 (not_369_out, F4);
  not not_370 (not_370_out, F3);
  not not_371 (not_371_out, F2);
  not not_372 (not_372_out, F1);
  not not_373 (not_373_out, F0);
  not not_374 (not_374_out, OP5);
  not not_375 (not_375_out, OP4);
  not not_376 (not_376_out, OP3);
  not not_377 (not_377_out, OP2);
  not not_378 (not_378_out, OP1);
  not not_379 (not_379_out, OP0);
  not not_380 (not_380_out, F4);
  not not_381 (not_381_out, F3);
  not not_382 (not_382_out, F2);
  not not_383 (not_383_out, F1);
  not not_384 (not_384_out, OP5);
  not not_385 (not_385_out, OP4);
  not not_386 (not_386_out, OP3);
  not not_387 (not_387_out, OP2);
  not not_388 (not_388_out, OP1);
  not not_389 (not_389_out, OP0);
  not not_390 (not_390_out, F4);
  not not_391 (not_391_out, F3);
  not not_392 (not_392_out, F2);
  not not_393 (not_393_out, F0);
  not not_394 (not_394_out, OP5);
  not not_395 (not_395_out, OP4);
  not not_396 (not_396_out, OP3);
  not not_397 (not_397_out, OP2);
  not not_398 (not_398_out, OP1);
  not not_399 (not_399_out, OP0);
  not not_400 (not_400_out, F4);
  not not_401 (not_401_out, F3);
  not not_402 (not_402_out, F1);
  not not_403 (not_403_out, F0);
  not not_404 (not_404_out, OP5);
  not not_405 (not_405_out, OP4);
  not not_406 (not_406_out, OP3);
  not not_407 (not_407_out, OP2);
  not not_408 (not_408_out, OP1);
  not not_409 (not_409_out, OP0);
  not not_410 (not_410_out, F4);
  not not_411 (not_411_out, F3);
  not not_412 (not_412_out, F1);
  not not_413 (not_413_out, OP5);
  not not_414 (not_414_out, OP4);
  not not_415 (not_415_out, OP3);
  not not_416 (not_416_out, OP2);
  not not_417 (not_417_out, OP1);
  not not_418 (not_418_out, OP0);
  not not_419 (not_419_out, F4);
  not not_420 (not_420_out, F3);
  not not_421 (not_421_out, OP5);
  not not_422 (not_422_out, OP4);
  not not_423 (not_423_out, OP3);
  not not_424 (not_424_out, OP2);
  not not_425 (not_425_out, OP1);
  not not_426 (not_426_out, OP0);
  not not_427 (not_427_out, F4);
  not not_428 (not_428_out, F2);
  not not_429 (not_429_out, F0);
  not not_430 (not_430_out, OP5);
  not not_431 (not_431_out, OP4);
  not not_432 (not_432_out, OP3);
  not not_433 (not_433_out, OP2);
  not not_434 (not_434_out, OP1);
  not not_435 (not_435_out, OP0);
  not not_436 (not_436_out, F4);
  not not_437 (not_437_out, F2);
  not not_438 (not_438_out, OP5);
  not not_439 (not_439_out, OP4);
  not not_440 (not_440_out, OP3);
  not not_441 (not_441_out, OP2);
  not not_442 (not_442_out, OP1);
  not not_443 (not_443_out, OP0);
  not not_444 (not_444_out, F5);
  not not_445 (not_445_out, F4);
  not not_446 (not_446_out, F2);
  not not_447 (not_447_out, F1);
  not not_448 (not_448_out, F0);
  not not_449 (not_449_out, OP5);
  not not_450 (not_450_out, OP4);
  not not_451 (not_451_out, OP3);
  not not_452 (not_452_out, OP1);
  not not_453 (not_453_out, OP0);
  not not_454 (not_454_out, OP5);
  not not_455 (not_455_out, OP4);
  not not_456 (not_456_out, OP3);
  not not_457 (not_457_out, OP1);
  not not_458 (not_458_out, OP5);
  not not_459 (not_459_out, OP4);
  not not_460 (not_460_out, OP3);
  not not_461 (not_461_out, OP2);
  not not_462 (not_462_out, OP1);
  not not_463 (not_463_out, OP0);
  not not_464 (not_464_out, F5);
  not not_465 (not_465_out, F4);
  not not_466 (not_466_out, F2);
  not not_467 (not_467_out, F1);
  not not_468 (not_468_out, F0);
  not not_469 (not_469_out, OP5);
  not not_470 (not_470_out, OP4);
  not not_471 (not_471_out, OP3);
  not not_472 (not_472_out, OP2);
  not not_473 (not_473_out, OP1);
  not not_474 (not_474_out, OP0);
  not not_475 (not_475_out, F5);
  not not_476 (not_476_out, F4);
  not not_477 (not_477_out, F2);
  not not_478 (not_478_out, F1);
  not not_479 (not_479_out, F0);
  not not_480 (not_480_out, OP5);
  not not_481 (not_481_out, OP4);
  not not_482 (not_482_out, OP3);
  not not_483 (not_483_out, OP2);
  not not_484 (not_484_out, OP0);
  not not_485 (not_485_out, OP5);
  not not_486 (not_486_out, OP4);
  not not_487 (not_487_out, OP3);
  not not_488 (not_488_out, OP2);
  not not_489 (not_489_out, OP5);
  not not_490 (not_490_out, OP4);
  not not_491 (not_491_out, OP3);
  not not_492 (not_492_out, OP2);
  not not_493 (not_493_out, OP4);
  not not_494 (not_494_out, OP2);
  not not_495 (not_495_out, OP1);
  not not_496 (not_496_out, OP5);
  not not_497 (not_497_out, OP4);
  not not_498 (not_498_out, OP3);
  and and_1 (MemToReg, OP5, not_1_out, not_2_out, not_3_out, OP1, OP0);
  and and_2 (and_2_out, OP5, not_4_out, OP3, not_5_out, OP1, OP0);
  and and_3 (and_3_out, OP5, not_6_out, OP3, not_7_out, not_8_out, OP0);
  and and_4 (and_4_out, not_9_out, not_10_out, OP3, not_11_out, not_12_out, not_13_out);
  and and_5 (and_5_out, not_14_out, not_15_out, OP3, OP2, not_16_out, not_17_out);
  and and_6 (and_6_out, not_18_out, not_19_out, OP3, not_20_out, not_21_out, OP0);
  and and_7 (and_7_out, not_22_out, not_23_out, OP3, not_24_out, OP1, not_25_out);
  and and_8 (and_8_out, not_26_out, not_27_out, OP3, OP2, not_28_out, OP0);
  and and_9 (and_9_out, OP5, not_29_out, not_30_out, not_31_out, OP1, OP0);
  and and_10 (and_10_out, OP5, not_32_out, OP3, not_33_out, OP1, OP0);
  and and_11 (and_11_out, not_34_out, not_35_out, OP3, OP2, OP1, OP0);
  and and_12 (and_12_out, not_36_out, not_37_out, OP3, not_38_out, OP1, OP0);
  and and_13 (and_13_out, OP5, not_39_out, OP3, not_40_out, not_41_out, OP0);
  and and_14 (and_14_out, not_42_out, not_43_out, not_44_out, not_45_out, not_46_out, not_47_out, not_48_out, not_49_out, not_50_out, not_51_out, not_52_out, not_53_out);
  and and_15 (and_15_out, not_54_out, not_55_out, not_56_out, not_57_out, not_58_out, not_59_out, not_60_out, not_61_out, not_62_out, not_63_out, F1, F0);
  and and_16 (and_16_out, not_64_out, not_65_out, not_66_out, not_67_out, not_68_out, not_69_out, not_70_out, not_71_out, not_72_out, not_73_out, F1, not_74_out);
  and and_17 (and_17_out, not_75_out, not_76_out, not_77_out, not_78_out, not_79_out, not_80_out, F5, not_81_out, not_82_out, not_83_out, not_84_out, not_85_out);
  and and_18 (and_18_out, not_86_out, not_87_out, not_88_out, not_89_out, not_90_out, not_91_out, F5, not_92_out, not_93_out, not_94_out, not_95_out, F0);
  and and_19 (and_19_out, not_96_out, not_97_out, not_98_out, not_99_out, not_100_out, not_101_out, F5, not_102_out, not_103_out, not_104_out, F1, not_105_out);
  and and_20 (and_20_out, not_106_out, not_107_out, not_108_out, not_109_out, not_110_out, not_111_out, F5, not_112_out, not_113_out, F2, not_114_out, not_115_out);
  and and_21 (and_21_out, not_116_out, not_117_out, not_118_out, not_119_out, not_120_out, not_121_out, F5, not_122_out, not_123_out, F2, not_124_out, F0);
  and and_22 (and_22_out, not_125_out, not_126_out, not_127_out, not_128_out, not_129_out, not_130_out, F5, not_131_out, not_132_out, F2, F1, F0);
  and and_23 (and_23_out, not_133_out, not_134_out, not_135_out, not_136_out, not_137_out, not_138_out, F5, not_139_out, F3, not_140_out, F1, not_141_out);
  and and_24 (and_24_out, not_142_out, not_143_out, not_144_out, not_145_out, not_146_out, not_147_out, F5, not_148_out, F3, not_149_out, F1, F0);
  and and_25 (and_25_out, not_150_out, not_151_out, not_152_out, not_153_out, OP1, OP0);
  and and_26 (and_26_out, not_154_out, not_155_out, OP3, not_156_out, not_157_out, not_158_out);
  and and_27 (and_27_out, not_159_out, not_160_out, OP3, OP2, not_161_out, not_162_out);
  and and_28 (and_28_out, not_163_out, not_164_out, OP3, not_165_out, not_166_out, OP0);
  and and_29 (and_29_out, not_167_out, not_168_out, OP3, not_169_out, OP1, not_170_out);
  and and_30 (and_30_out, not_171_out, not_172_out, OP3, OP2, not_173_out, OP0);
  and and_31 (and_31_out, OP5, not_174_out, not_175_out, not_176_out, OP1, OP0);
  and and_32 (and_32_out, not_177_out, not_178_out, OP3, OP2, OP1, OP0);
  and and_33 (and_33_out, not_179_out, not_180_out, OP3, not_181_out, OP1, OP0);
  and and_34 (LUI, not_182_out, not_183_out, OP3, OP2, OP1, OP0);
  and and_35 (SysCALL, not_184_out, not_185_out, not_186_out, not_187_out, not_188_out, not_189_out, not_190_out, not_191_out, F3, F2, not_192_out, not_193_out);
  and and_36 (and_36_out, not_194_out, not_195_out, not_196_out, not_197_out, not_198_out, not_199_out, not_200_out, not_201_out);
  and and_37 (and_37_out, not_202_out, not_203_out, not_204_out, not_205_out, not_206_out, not_207_out, F5);
  and and_38 (and_38_out, not_208_out, not_209_out, not_210_out, not_211_out, not_212_out, not_213_out, F3, not_214_out, not_215_out);
  and and_39 (and_39_out, not_216_out, not_217_out, not_218_out, not_219_out, F1, not_220_out, not_221_out, not_222_out);
  and and_40 (and_40_out, not_223_out, not_224_out, not_225_out, not_226_out, F1, not_227_out, not_228_out, F5);
  and and_41 (and_41_out, not_229_out, not_230_out, not_231_out, OP3, not_232_out);
  and and_42 (and_42_out, not_233_out, not_234_out, OP3, not_235_out, not_236_out);
  and and_43 (and_43_out, not_237_out, OP3, not_238_out, not_239_out);
  and and_44 (and_44_out, not_240_out, OP2, not_241_out, not_242_out, not_243_out);
  and and_45 (and_45_out, not_244_out, OP2, not_245_out, not_246_out);
  and and_46 (and_46_out, OP0, OP1, not_247_out, not_248_out, OP5);
  and and_47 (and_47_out, not_249_out, not_250_out, not_251_out, not_252_out, not_253_out, not_254_out, not_255_out, not_256_out, not_257_out);
  and and_48 (and_48_out, not_258_out, not_259_out, not_260_out, not_261_out, not_262_out, not_263_out, not_264_out, not_265_out, F5);
  and and_49 (and_49_out, not_266_out, not_267_out, not_268_out, not_269_out, not_270_out, not_271_out, not_272_out, F2, F3, not_273_out, not_274_out);
  and and_50 (and_50_out, not_275_out, not_276_out, not_277_out, not_278_out, not_279_out, F1, not_280_out, not_281_out, not_282_out, not_283_out);
  and and_51 (and_51_out, not_284_out, not_285_out, not_286_out, not_287_out, not_288_out, F1, not_289_out, F3, not_290_out, F5);
  and and_52 (and_52_out, not_291_out, not_292_out, not_293_out, not_294_out, not_295_out, F0, F2, not_296_out, not_297_out, F5);
  and and_53 (and_53_out, not_298_out, OP2, not_299_out, not_300_out, not_301_out);
  and and_54 (and_54_out, OP0, not_302_out, OP3, not_303_out, OP5);
  and and_55 (and_55_out, OP0, OP1, OP3, not_304_out, not_305_out);
  and and_56 (and_56_out, not_306_out, not_307_out, OP3, not_308_out, not_309_out, not_310_out);
  and and_57 (and_57_out, not_311_out, not_312_out, OP3, not_313_out, not_314_out, OP0);
  and and_58 (and_58_out, not_315_out, not_316_out, OP3, not_317_out, OP1, not_318_out);
  and and_59 (and_59_out, OP5, not_319_out, not_320_out, not_321_out, OP1, OP0);
  and and_60 (and_60_out, OP5, not_322_out, OP3, not_323_out, OP1, OP0);
  and and_61 (and_61_out, not_324_out, not_325_out, OP3, not_326_out, OP1, OP0);
  and and_62 (and_62_out, OP5, not_327_out, OP3, not_328_out, not_329_out, OP0);
  and and_63 (and_63_out, not_330_out, not_331_out, not_332_out, not_333_out, not_334_out, not_335_out, not_336_out, not_337_out, not_338_out, not_339_out, not_340_out, not_341_out);
  and and_64 (and_64_out, not_342_out, not_343_out, not_344_out, not_345_out, not_346_out, not_347_out, not_348_out, not_349_out, not_350_out, not_351_out, F1, F0);
  and and_65 (and_65_out, not_352_out, not_353_out, not_354_out, not_355_out, not_356_out, not_357_out, not_358_out, not_359_out, not_360_out, not_361_out, F1, not_362_out);
  and and_66 (and_66_out, not_363_out, not_364_out, not_365_out, not_366_out, not_367_out, not_368_out, F5, not_369_out, not_370_out, not_371_out, not_372_out, not_373_out);
  and and_67 (and_67_out, not_374_out, not_375_out, not_376_out, not_377_out, not_378_out, not_379_out, F5, not_380_out, not_381_out, not_382_out, not_383_out, F0);
  and and_68 (and_68_out, not_384_out, not_385_out, not_386_out, not_387_out, not_388_out, not_389_out, F5, not_390_out, not_391_out, not_392_out, F1, not_393_out);
  and and_69 (and_69_out, not_394_out, not_395_out, not_396_out, not_397_out, not_398_out, not_399_out, F5, not_400_out, not_401_out, F2, not_402_out, not_403_out);
  and and_70 (and_70_out, not_404_out, not_405_out, not_406_out, not_407_out, not_408_out, not_409_out, F5, not_410_out, not_411_out, F2, not_412_out, F0);
  and and_71 (and_71_out, not_413_out, not_414_out, not_415_out, not_416_out, not_417_out, not_418_out, F5, not_419_out, not_420_out, F2, F1, F0);
  and and_72 (and_72_out, not_421_out, not_422_out, not_423_out, not_424_out, not_425_out, not_426_out, F5, not_427_out, F3, not_428_out, F1, not_429_out);
  and and_73 (and_73_out, not_430_out, not_431_out, not_432_out, not_433_out, not_434_out, not_435_out, F5, not_436_out, F3, not_437_out, F1, F0);
  and and_74 (and_74_out, not_438_out, not_439_out, not_440_out, not_441_out, not_442_out, not_443_out, not_444_out, not_445_out, F3, not_446_out, not_447_out, not_448_out);
  and and_75 (BEQ, not_449_out, not_450_out, not_451_out, OP2, not_452_out, not_453_out);
  and and_76 (BNE, not_454_out, not_455_out, not_456_out, OP2, not_457_out, OP0);
  and and_77 (JR, not_458_out, not_459_out, not_460_out, not_461_out, not_462_out, not_463_out, not_464_out, not_465_out, F3, not_466_out, not_467_out, not_468_out);
  and and_78 (and_78_out, not_469_out, not_470_out, not_471_out, not_472_out, not_473_out, not_474_out, not_475_out, not_476_out, F3, not_477_out, not_478_out, not_479_out);
  and and_79 (and_79_out, not_480_out, not_481_out, not_482_out, not_483_out, OP1, not_484_out);
  and and_80 (and_80_out, not_485_out, not_486_out, not_487_out, not_488_out, OP1, OP0);
  and and_81 (JAL, not_489_out, not_490_out, not_491_out, not_492_out, OP1, OP0);
  and and_82 (SH, OP5, not_493_out, OP3, not_494_out, not_495_out, OP0);
  and and_83 (BGTZ, not_496_out, not_497_out, not_498_out, OP2, OP1, OP0);
  or or_1 (MemWrite, and_2_out, and_3_out);
  or or_2 (ALU_SRC, and_4_out, and_5_out, and_6_out, and_7_out, and_8_out, and_9_out, and_10_out, and_11_out, and_12_out, and_13_out);
  or or_3 (RsUsed, and_36_out, and_37_out, and_38_out, and_39_out, and_40_out, and_41_out, and_42_out, and_43_out, and_44_out, and_45_out, and_46_out);
  or or_4 (RtUsed, and_47_out, and_48_out, and_49_out, and_50_out, and_51_out, and_52_out, and_53_out, and_54_out, and_55_out);
  or or_5 (SignedExt, and_56_out, and_57_out, and_58_out, and_59_out, and_60_out, and_61_out, and_62_out);
  or or_6 (JUMP, and_78_out, and_79_out, and_80_out);
  or or_7 (RegWrite, and_14_out, and_15_out, and_16_out, and_17_out, and_18_out, and_19_out, and_20_out, and_21_out, and_22_out, and_23_out, and_24_out, and_25_out, and_26_out, and_27_out, and_28_out, and_29_out, and_30_out, and_31_out, and_32_out, and_33_out);
  or or_8 (RegDst, and_63_out, and_64_out, and_65_out, and_66_out, and_67_out, and_68_out, and_69_out, and_70_out, and_71_out, and_72_out, and_73_out, and_74_out);
endmodule

// ALU
module MIPS_ALU (
  input  [4:0] shamt,
  input  [31:0] X,
  input  [31:0] Y,
  input  [3:0] AluOP,
  output Equal,
  output [31:0] Result,
  output [31:0] Result_2
);

  wire [0:0] comparator_1_lt, comparator_2_lt;
  wire [31:0] adder_1_out, AND_out, divider_1_out, divider_1_rem, multiplier_1_cout, multiplier_1_out,
       NOR_out, OR_out, shifter_1_out, shifter_2_out, shifter_3_out, subtractor_1_out, XOR_out;

  assign AND_out = X & Y;  // AND_Gate AND, 32 bits wide
  assign OR_out = X | Y;  // OR_Gate OR, 32 bits wide
  Shifter #(.width(32), .shift("ll")) shifter_1 (.in(Y), .\dist (shamt), .out(shifter_1_out));
  Shifter #(.width(32), .shift("ar")) shifter_2 (.in(Y), .\dist (shamt), .out(shifter_2_out));
  Shifter #(.width(32), .shift("lr")) shifter_3 (.in(Y), .\dist (shamt), .out(shifter_3_out));
  Multiplier #(.width(32)) multiplier_1 (.a(X), .b(Y), .out(multiplier_1_out), .cout(multiplier_1_cout));  // open: cin
  Divider #(.width(32)) divider_1 (.a(X), .b(Y), .out(divider_1_out), .rem(divider_1_rem));  // open: upper
  Adder #(.width(32)) adder_1 (.a(X), .b(Y), .out(adder_1_out));  // open: cin, cout
  Subtractor #(.width(32)) subtractor_1 (.a(X), .b(Y), .out(subtractor_1_out));  // open: bin, bout
  assign XOR_out = X ^ Y;  // XOR_Gate XOR, 32 bits wide
  assign NOR_out = ~(X | Y);  // NOR_Gate NOR, 32 bits wide
  Comparator #(.width(32), .mode("twosComplement")) comparator_1 (
    .a(X), .b(Y), .eq(Equal), .lt(comparator_1_lt[0]));  // open: gt
  Comparator #(.width(32), .mode("unsigned")) comparator_2 (.a(X), .b(Y), .lt(comparator_2_lt[0]));  // open: gt, eq
  Multiplexer #(.select(4), .width(32), .disabled("Z"), .enable("false")) multiplexer_1 (
    .in0(shifter_1_out), .in1(shifter_2_out), .in2(shifter_3_out), .in3(multiplier_1_out),
    .in4(divider_1_out), .in5(adder_1_out), .in6(subtractor_1_out), .in7(AND_out), .in8(OR_out),
    .in9(XOR_out), .in10(NOR_out), .in11({{31{1'b0}}, comparator_1_lt[0]}),
    .in12({{31{1'b0}}, comparator_2_lt[0]}), .in13({32{1'b0}}), .in14({32{1'b0}}), .in15({32{1'b0}}),
    .out(Result), .sel(AluOP));
  Multiplexer #(.select(4), .width(32), .disabled("Z"), .enable("false")) multiplexer_2 (
    .in0({32{1'b0}}), .in1({32{1'b0}}), .in2({32{1'b0}}), .in3(multiplier_1_cout), .in4(divider_1_rem),
    .in5({32{1'b0}}), .in6({32{1'b0}}), .in7({32{1'b0}}), .in8({32{1'b0}}), .in9({32{1'b0}}),
    .in10({32{1'b0}}), .in11({32{1'b0}}), .in12({32{1'b0}}), .in13({32{1'b0}}), .in14({32{1'b0}}),
    .in15({32{1'b0}}), .out(Result_2), .sel(AluOP));

  // Other names for the same wires on the sheet: Result2[31:0] = Result_2; S[3:0] = AluOP

  // Notes on the sheet:
  //   不要改变此引脚区域内容，也不要改变ALU封装形式
  //   输入引脚
  //   输出引脚
endmodule

module MIPS_Regifile (
  input  [31:0] Din,
  input  Clk,
  input  WE,
  input  [4:0] R1_num,
  input  [4:0] W_num,
  input  [4:0] R2_num,
  output [31:0] R1,
  output [31:0] R2
);

  // RegisterFile registerfile_1: pin names not known; wires that end beside it: Din, Clk, WE, W_num, R1_num, R2_num, R1, R2
endmodule

module \理想流水线  (
  output RegWrite,
  output MemWrite,
  output [31:0] IF_PC,
  output [31:0] ID_PC,
  output [31:0] EX_PC,
  output [31:0] M_PC,
  output [31:0] WB_PC,
  output [31:0] RDin,
  output [31:0] MDin,
  output [31:0] LedData
);

  wire and_1_out, and_3_out, and_4_out, and_5_out, CLK, clock_1_out, clock_2_out, comparator_1_eq,
       comparator_2_eq, comparator_2_lt, comparator_3_gt, d_ff_1_q, ex_mem_1_jal_2, ex_mem_1_memtoreg_2,
       ex_mem_1_regdst_2, ex_mem_1_regwrite_2, ex_mem_1_sh_2, ex_mem_1_syscall_2, Go, halt,
       id_ex_1_alusrcb_2, id_ex_1_beq_2, id_ex_1_bgtz_2, id_ex_1_bne_2, id_ex_1_jal_2, id_ex_1_jmp_2,
       id_ex_1_jr_2, id_ex_1_memtoreg_2, id_ex_1_memwrite_2, id_ex_1_regdst_2, id_ex_1_regwrite_2,
       id_ex_1_sh_2, id_ex_1_syscall_2, IR1, IR2, IR3, JAL, LED, mem_wb_1_memtoreg_2, mips_alu_1_equal,
       nand_1_out, not_1_out, not_3_out, not_4_out, not_5_out, not_6_out, not_7_out, or_1_out, RegDst, RST,
       SignedExt, Syscall, W1, W2, W3, \单周期硬布线控制器_1_alu_src , \单周期硬布线控制器_1_beq , \单周期硬布线控制器_1_bgtz ,
       \单周期硬布线控制器_1_bne , \单周期硬布线控制器_1_jal , \单周期硬布线控制器_1_jmp , \单周期硬布线控制器_1_memtoreg ,
       \单周期硬布线控制器_1_memwrite , \单周期硬布线控制器_1_regdst , \单周期硬布线控制器_1_regwrite , \单周期硬布线控制器_1_sh ,
       \单周期硬布线控制器_1_signedext ;
  wire [3:0] id_ex_1_aluop_2, \单周期硬布线控制器_1_alu_op ;
  wire [4:0] multiplexer_4_out, multiplexer_5_out, multiplexer_6_out, multiplexer_7_out, WB_rd, WB_rt;
  wire [12:0] CNT_num;
  wire [15:0] \LoadUse次数 , ram_1_data, ram_1_data_2, \总周期数 , \插入气泡数 , \无条件分支数 , \条件分支成功数 ;
  wire [27:2] \无条件跳转 ;
  wire [31:0] a0, bit_extender_1_out, bit_extender_2_out, EX_IR, ex_mem_1_alu_2, ex_mem_1_pc_4_2,
       ex_mem_1_r2_2, id_ex_1_pc_4_2, id_ex_1_r2_2, ID_IR, if_id_1_pc_4_2, IF_IR, JALPC, JRPC, MEM_IR,
       mem_wb_1_alu_2, mem_wb_1_ir_2, mem_wb_1_md_2, mips_alu_1_result, multiplexer_1_out, multiplexer_2_out,
       multiplexer_3_out, multiplexer_10_out, multiplexer_11_out, multiplexer_13_out, offset, PC_4,
       shifter_1_out, v0, WB_IR, \条件跳转 ;

  Button \u_总复位  (.out(RST));
  Button _1 (.out(IR1));
  Button _2 (.out(IR2));
  Button _3 (.out(IR3));
  // Probe on \总周期数 
  // Probe on \总周期数 
  Button \u_继续运行  (.out(Go));
  LED #(.active("true")) led_1 (.in(W1));
  LED #(.active("true")) led_2 (.in(W2));
  LED #(.active("true")) led_3 (.in(W3));
  Hex_Digit_Display hex_digit_display_1 (.value(LedData[31:28]));  // open: dp
  // Probe on IF_PC[19:0]
  // Mips_Probe mips_probe_1: pin names not known; wires that end beside it: IF_IR
  Comparator #(.width(32), .mode("twosComplement")) comparator_1 (
    .a(v0), .b(32'h32), .eq(comparator_1_eq));  // open: gt, lt
  Hex_Digit_Display hex_digit_display_2 (.value(LedData[27:24]));  // open: dp
  Hex_Digit_Display hex_digit_display_3 (.value(LedData[23:20]));  // open: dp
  // Probe on ID_PC[19:0]
  // Mips_Probe mips_probe_2: pin names not known; wires that end beside it: ID_IR
  and and_1 (and_1_out, Syscall, comparator_1_eq);
  and and_2 (LED, Syscall, not_1_out);
  not not_1 (not_1_out, comparator_1_eq);
  Hex_Digit_Display hex_digit_display_4 (.value(LedData[15:12]));  // open: dp
  Hex_Digit_Display hex_digit_display_5 (.value(LedData[19:16]));  // open: dp
  not not_2 (halt, and_1_out);
  Hex_Digit_Display hex_digit_display_6 (.value(LedData[11:8]));  // open: dp
  Hex_Digit_Display hex_digit_display_7 (.value(LedData[7:4]));  // open: dp
  Clock #(.highDuration(1), .lowDuration(1)) clock_1 (.out(clock_1_out));
  // Probe on EX_PC[19:0]
  // Mips_Probe mips_probe_3: pin names not known; wires that end beside it: clock_1_out, EX_IR, CLK
  Multiplexer #(.select(1), .width(32), .disabled("Z"), .enable("false")) multiplexer_1 (
    .in0(PC_4), .in1(\条件跳转 ), .out(multiplexer_1_out), .sel(or_1_out));
  Multiplexer #(.select(1), .width(32), .disabled("Z"), .enable("false")) multiplexer_2 (
    .in0(multiplexer_1_out), .in1({PC_4[31:28], \无条件跳转 , 2'b00}), .out(multiplexer_2_out), .sel(id_ex_1_jmp_2));
  Hex_Digit_Display hex_digit_display_8 (.value(LedData[3:0]));  // open: dp
  Multiplexer #(.select(1), .width(32), .disabled("Z"), .enable("false")) multiplexer_3 (
    .in0(multiplexer_2_out), .in1(JRPC), .out(multiplexer_3_out), .sel(id_ex_1_jr_2));
  // Probe on \总周期数 
  // Probe on M_PC[19:0]
  // Mips_Probe mips_probe_4: pin names not known; wires that end beside it: MEM_IR
  // Probe on \总周期数 
  // Probe on \无条件分支数 
  // Probe on \条件分支成功数 
  // Probe on \插入气泡数 
  // Probe on \LoadUse次数 
  Register #(.width(32), .trigger("rising"), .Select("low")) PC (
    .D(multiplexer_3_out), .en(halt), .Q(IF_PC), .clk(CLK), .clr(RST));
  // Probe on IF_PC[11:0]
  // Probe on WB_PC[19:0]
  // Mips_Probe mips_probe_5: pin names not known; wires that end beside it: WB_IR
  Adder #(.width(32)) adder_1 (.a(IF_PC), .b(32'h4), .out(PC_4));  // open: cin, cout
  // Probe on EX_PC[11:0]
  // Probe on ID_PC[11:0]
  // Probe on M_PC[11:0]
  D_Flip_Flop #(.trigger("high"), .Pre_Clr_Positions("LEGACY"), .NegatePresetClear("false"), .enable("true"), .NewFFLayout("false")) d_ff_1 (.Q(d_ff_1_q));  // open: clk, D, Qn, preset, en, reset
  // Probe on 13'hc
  ROM #(.addrWidth(10), .dataWidth(32), .Select("high")) rom_1 (.addr(IF_PC[11:2]), .data(IF_IR));
  not not_3 (not_3_out, halt);
  // Probe on WB_PC[11:0]
  Comparator #(.width(13), .mode("twosComplement")) comparator_2 (
    .a(CNT_num), .b(13'hc), .eq(comparator_2_eq), .lt(comparator_2_lt));  // open: gt
  Clock #(.highDuration(1), .lowDuration(1)) clock_2 (.out(clock_2_out));
  IF_ID if_id_1 (
    .CLK(CLK), .\使能端_低电平有效 (not_3_out), .PC(IF_PC), .IR(IF_IR), .PC_4(PC_4), .PC_2(ID_PC), .IR_2(ID_IR),
    .PC_4_2(if_id_1_pc_4_2));  // open: 同步清0_高电平有效
  nand nand_1 (nand_1_out, d_ff_1_q, comparator_2_eq);
  Counter #(.width(13), .max('h1fff), .ongoal("stay"), .trigger("rising"), .behavior("old")) counter_1 (
    .count(comparator_2_lt), .Q(CNT_num), .clk(clock_2_out));  // open: load, D, carry, clr, preset
  assign CLK = nand_1_out ? clock_2_out : 1'bz;  // Controlled_Buffer controlled_buffer_1
  Pull_Resistor #(.pull(1)) pull_resistor_1 (.node(CLK));
  Button button_1 (.out(RST));
  Counter #(.width(16), .max('hffff), .ongoal("wrap"), .trigger("rising"), .behavior("new")) counter_2 (
    .count(halt), .Q(\总周期数 ), .clk(CLK), .clr(RST));  // open: load, D, carry, preset, down
  \单周期硬布线控制器  \u_单周期硬布线控制器_1  (
    .Func(ID_IR[5:0]), .OP(ID_IR[31:26]), .ALU_OP(\单周期硬布线控制器_1_alu_op ), .MemToReg(\单周期硬布线控制器_1_memtoreg ),
    .MemWrite(\单周期硬布线控制器_1_memwrite ), .ALU_SRC(\单周期硬布线控制器_1_alu_src ), .RegWrite(\单周期硬布线控制器_1_regwrite ),
    .SysCALL(Syscall), .SignedExt(\单周期硬布线控制器_1_signedext ), .RegDst(\单周期硬布线控制器_1_regdst ), .JR(Syscall),
    .JMP(\单周期硬布线控制器_1_jmp ), .Beq(\单周期硬布线控制器_1_beq ), .JAL(\单周期硬布线控制器_1_jal ), .Bne(\单周期硬布线控制器_1_bne ),
    .SH(\单周期硬布线控制器_1_sh ), .BGTZ(\单周期硬布线控制器_1_bgtz ));  // open: RtUsed, RsUsed, LUI
  Multiplexer #(.select(1), .width(5), .disabled("Z"), .enable("false")) multiplexer_4 (
    .in0(WB_rt), .in1(WB_rd), .out(multiplexer_4_out), .sel(RegDst));
  Multiplexer #(.select(1), .width(5), .disabled("Z"), .enable("false")) multiplexer_5 (
    .in0(ID_IR[25:21]), .in1(5'b00010), .out(multiplexer_5_out), .sel(Syscall));
  Multiplexer #(.select(1), .width(5), .disabled("Z"), .enable("false")) multiplexer_6 (
    .in0(ID_IR[20:16]), .in1(5'b00100), .out(multiplexer_6_out), .sel(Syscall));
  Multiplexer #(.select(1), .width(5), .disabled("Z"), .enable("false")) multiplexer_7 (
    .in0(multiplexer_4_out), .in1({5{1'b1}}), .out(multiplexer_7_out), .sel(JAL));
  Multiplexer #(.select(1), .width(32), .disabled("Z"), .enable("false")) multiplexer_8 (
    .in0(multiplexer_13_out), .in1(JALPC), .out(RDin), .sel(JAL));
  MIPS_Regifile mips_regifile_1 (
    .Din(RDin), .Clk(CLK), .R1(v0), .R2(a0), .WE(RegWrite), .W_num(multiplexer_7_out),
    .R1_num(multiplexer_5_out), .R2_num(multiplexer_6_out));
  assign bit_extender_1_out = {{16{1'b0}}, \无条件跳转 [17:2]};  // Bit_Extender bit_extender_1
  assign bit_extender_2_out = {{16{\无条件跳转 [17]}}, \无条件跳转 [17:2]};  // Bit_Extender bit_extender_2
  Multiplexer #(.select(1), .width(32), .disabled("Z"), .enable("false")) multiplexer_9 (
    .in0(bit_extender_1_out), .in1(bit_extender_2_out), .out(offset), .sel(SignedExt));
  ID_EX id_ex_1 (
    .CLK(CLK), .\使能端_低电平有效 (not_4_out), .PC(ID_PC), .IR(ID_IR), .PC_4(if_id_1_pc_4_2), .R1(v0), .R2(a0),
    .Imm26(ID_IR[25:0]), .BGTZ(\单周期硬布线控制器_1_bgtz ), .BEQ(\单周期硬布线控制器_1_beq ), .BNE(\单周期硬布线控制器_1_bne ),
    .JR(Syscall), .JMP(\单周期硬布线控制器_1_jmp ), .SignedExt(\单周期硬布线控制器_1_signedext ), .Syscall(Syscall),
    .MemToReg(\单周期硬布线控制器_1_memtoreg ), .RegWrite(\单周期硬布线控制器_1_regwrite ), .RegDst(\单周期硬布线控制器_1_regdst ),
    .JAL(\单周期硬布线控制器_1_jal ), .MemWrite(\单周期硬布线控制器_1_memwrite ), .SH(\单周期硬布线控制器_1_sh ),
    .AluSrcB(\单周期硬布线控制器_1_alu_src ), .AluOP(\单周期硬布线控制器_1_alu_op ), .PC_2(EX_PC), .IR_2(EX_IR),
    .PC_4_2(id_ex_1_pc_4_2), .R1_2(JRPC), .R2_2(id_ex_1_r2_2), .Imm26_2(\无条件跳转 ), .BGTZ_2(id_ex_1_bgtz_2),
    .BEQ_2(id_ex_1_beq_2), .BNE_2(id_ex_1_bne_2), .JR_2(id_ex_1_jr_2), .JMP_2(id_ex_1_jmp_2),
    .SignedExt_2(SignedExt), .Syscall_2(id_ex_1_syscall_2), .MemToReg_2(id_ex_1_memtoreg_2),
    .RegWrite_2(id_ex_1_regwrite_2), .RegDst_2(id_ex_1_regdst_2), .JAL_2(id_ex_1_jal_2),
    .MemWrite_2(id_ex_1_memwrite_2), .SH_2(id_ex_1_sh_2), .AluSrcB_2(id_ex_1_alusrcb_2),
    .AluOP_2(id_ex_1_aluop_2));  // open: 同步清0_高电平有效, ForwardRs, ForwardRs_2, ForwardRt, ForwardRt_2, LUI, LUI_2
  not not_4 (not_4_out, halt);
  Shifter #(.width(32), .shift("ll")) shifter_1 (.in(offset), .\dist (5'b00010), .out(shifter_1_out));
  Adder #(.width(32)) adder_2 (.a(shifter_1_out), .b(PC_4), .out(\条件跳转 ));  // open: cin, cout
  Comparator #(.width(32), .mode("twosComplement")) comparator_3 (
    .a(JRPC), .b({32{1'b0}}), .gt(comparator_3_gt));  // open: eq, lt
  and and_3 (and_3_out, id_ex_1_bgtz_2, comparator_3_gt);
  Multiplexer #(.select(1), .width(32), .disabled("Z"), .enable("false")) multiplexer_10 (
    .in0(id_ex_1_r2_2), .in1(offset), .out(multiplexer_10_out), .sel(id_ex_1_alusrcb_2));
  and and_4 (and_4_out, id_ex_1_beq_2, mips_alu_1_equal);
  not not_5 (not_5_out, mips_alu_1_equal);
  MIPS_ALU mips_alu_1 (
    .X(JRPC), .Y(multiplexer_10_out), .AluOP(id_ex_1_aluop_2), .Equal(mips_alu_1_equal),
    .Result(mips_alu_1_result), .shamt(\无条件跳转 [12:8]));  // open: Result_2
  Register #(.width(32), .trigger("rising"), .Select("low")) register_1 (
    .D(id_ex_1_r2_2), .en(LED), .Q(LedData), .clk(CLK));  // open: clr
  and and_5 (and_5_out, id_ex_1_bne_2, not_5_out);
  or or_1 (or_1_out, and_3_out, and_4_out, and_5_out);
  EX_MEM ex_mem_1 (
    .CLK(CLK), .\使能端_低电平有效 (not_6_out), .IR(EX_IR), .PC_4(id_ex_1_pc_4_2), .R2(id_ex_1_r2_2),
    .Alu(mips_alu_1_result), .Syscall(id_ex_1_syscall_2), .MemToReg(id_ex_1_memtoreg_2),
    .RegWrite(id_ex_1_regwrite_2), .RegDst(id_ex_1_regdst_2), .JAL(id_ex_1_jal_2),
    .MemWrite(id_ex_1_memwrite_2), .SH(id_ex_1_sh_2), .PC_2(M_PC), .IR_2(MEM_IR), .PC_4_2(ex_mem_1_pc_4_2),
    .R2_2(ex_mem_1_r2_2), .Alu_2(ex_mem_1_alu_2), .Syscall_2(ex_mem_1_syscall_2),
    .MemToReg_2(ex_mem_1_memtoreg_2), .RegWrite_2(ex_mem_1_regwrite_2), .RegDst_2(ex_mem_1_regdst_2),
    .JAL_2(ex_mem_1_jal_2), .MemWrite_2(MemWrite), .SH_2(ex_mem_1_sh_2), .PC(EX_PC));  // open: 同步清0_高电平有效
  not not_6 (not_6_out, halt);
  Multiplexer #(.select(1), .width(32), .disabled("Z"), .enable("false")) multiplexer_11 (
    .in0({ram_1_data, ex_mem_1_r2_2[15:0]}), .in1({ex_mem_1_r2_2[15:0], ram_1_data_2}),
    .out(multiplexer_11_out), .sel(ex_mem_1_alu_2[1]));
  Multiplexer #(.select(1), .width(32), .disabled("Z"), .enable("false")) multiplexer_12 (
    .in0(ex_mem_1_r2_2), .in1(multiplexer_11_out), .out(MDin), .sel(ex_mem_1_sh_2));
  RAM #(.addrWidth(10), .dataWidth(32), .bus("separate"), .Select("high")) ram_1 (
    .addr(ex_mem_1_alu_2[11:2]), .din(MDin), .data({ram_1_data, ram_1_data_2}), .str(MemWrite), .clk(CLK),
    .clr(RST));  // open: sel, ld
  not not_7 (not_7_out, halt);
  MEM_WB mem_wb_1 (
    .CLK(CLK), .\使能端_低电平有效 (not_7_out), .IR(MEM_IR), .PC_4(ex_mem_1_pc_4_2), .MD({ram_1_data, ram_1_data_2}),
    .Alu(ex_mem_1_alu_2), .Syscall(ex_mem_1_syscall_2), .MemToReg(ex_mem_1_memtoreg_2),
    .RegWrite(ex_mem_1_regwrite_2), .RegDst(ex_mem_1_regdst_2), .JAL(ex_mem_1_jal_2), .PC_2(WB_PC),
    .IR_2({mem_wb_1_ir_2[31:21], WB_rt, WB_rd, mem_wb_1_ir_2[10:0]}), .PC_4_2(JALPC), .MD_2(mem_wb_1_md_2),
    .Alu_2(mem_wb_1_alu_2), .MemToReg_2(mem_wb_1_memtoreg_2), .RegWrite_2(RegWrite), .RegDst_2(RegDst),
    .JAL_2(JAL), .PC(M_PC));  // open: 同步清0_高电平有效, Syscall_2
  Multiplexer #(.select(1), .width(32), .disabled("Z"), .enable("false")) multiplexer_13 (
    .in0(mem_wb_1_alu_2), .in1(mem_wb_1_md_2), .out(multiplexer_13_out), .sel(mem_wb_1_memtoreg_2));

  // Other names for the same wires on the sheet: IR[31:0] = ID_IR; MEM_PC[31:0] = M_PC; PC[31:0] = IF_PC;
  //   无条件跳转[31:28] = PC_4[31:28]

  // Notes on the sheet:
  //   中断源
  //   时空图监测，可删除
  //   中断等待指示
  //   数码管输出
  //   控制位
  //   流水调试日志用
  //   暂停节拍，不能为0
  //   contents of rom_1 (hex, n*v repeats v):
  //   20100000 20110000 20120000 20130000 36100000 36310001 36520002 36730003 ae100000 ae110004 ae120008
  //   ae13000c 2002000a 20110000 20120000 20130000 c
  //   戳工具置1进入计数暂停模式，ctrl+k时钟自动运行到对应节拍暂停
  //   ctrl+k关闭时钟连续运行，将控制位置零，进入单步调试模式调试
  //   用这个时钟源需要去掉电路中的其他时钟源
  //   可计数暂停的时钟源
  //   指令存储器
  //   指令字
  //   OP
  //   Func
  //   rs
  //   rt
  //   imm26
  //   为方便自动评测，需要输出流水线各段保存的PC值，注意是PC不是PC+4，另外ID段寄存器写入信息，Mem段内存写入信息也要输出
  //   JMP
  //   JR
  //   OP
  //   Func
  //   Bne
  //   MemToReg
  //   MemWrite
  //   AluOP
  //   AluSrcB
  //   RegWrite
  //   JAL
  //   SH
  //   RegDst
  //   BGTZ
  //   Syscall
  //   rt
  //   rd
endmodule

module \气泡流水线  (
  output RegWrite,
  output MemWrite,
  output [31:0] IF_PC,
  output [31:0] ID_PC,
  output [31:0] EX_PC,
  output [31:0] M_PC,
  output [31:0] WB_PC,
  output [31:0] RDin,
  output [31:0] MDin,
  output [31:0] LedData
);

  wire and_2_out, and_3_out, and_4_out, and_5_out, and_6_out, BranchBubble, CLK, comparator_1_eq,
       comparator_1_lt, comparator_2_gt, comparator_3_eq, d_ff_1_q, DataHazzard, ex_mem_1_jal_2,
       ex_mem_1_memtoreg_2, ex_mem_1_regdst_2, ex_mem_1_sh_2, ex_mem_1_syscall_2, EX_RegWrite, Go, Halt,
       halt_t, id_ex_1_alusrcb_2, id_ex_1_beq_2, id_ex_1_bgtz_2, id_ex_1_bne_2, id_ex_1_jal_2, id_ex_1_jmp_2,
       id_ex_1_jr_2, id_ex_1_memtoreg_2, id_ex_1_memwrite_2, id_ex_1_regdst_2, id_ex_1_sh_2,
       id_ex_1_syscall_2, ID_EX_flush, IF_ID_EN, IF_ID_flush, IR1, IR2, IR3, JAL, LED, MEM_RegWrite,
       mem_wb_1_memtoreg_2, mips_alu_1_equal, nand_1_out, not_1_out, not_2_out, not_4_out, not_5_out,
       not_6_out, or_3_out, or_5_out, PC_EN, R1Used, R2Used, RegDst, RST, SignedExt, undriven, W1, W2, W3,
       \单周期硬布线控制器_1_alu_src , \单周期硬布线控制器_1_beq , \单周期硬布线控制器_1_bgtz , \单周期硬布线控制器_1_bne , \单周期硬布线控制器_1_jal ,
       \单周期硬布线控制器_1_jmp , \单周期硬布线控制器_1_jr , \单周期硬布线控制器_1_memtoreg , \单周期硬布线控制器_1_memwrite ,
       \单周期硬布线控制器_1_regdst , \单周期硬布线控制器_1_regwrite , \单周期硬布线控制器_1_sh , \单周期硬布线控制器_1_signedext ,
       \单周期硬布线控制器_1_syscall ;
  wire [3:0] id_ex_1_aluop_2, \单周期硬布线控制器_1_alu_op ;
  wire [4:0] EX_WriteReg_num, MEM_WriteReg_num, multiplexer_4_out, multiplexer_7_out, multiplexer_11_out,
       multiplexer_15_out, R1, R2;
  wire [12:0] CNT_num;
  wire [15:0] \LoadUse次数 , \总周期数 , \插入气泡数 , \无条件分支数 , \条件分支成功数 ;
  wire [27:2] \无条件跳转 ;
  wire [31:0] bit_extender_1_out, bit_extender_2_out, EX_IR, ex_mem_1_alu_2, ex_mem_1_pc_4_2, ex_mem_1_r2_2,
       EX_PC_4, id_ex_1_r2_2, ID_IR, if_id_1_pc_4_2, IF_IR, JALPC, JRPC, MEM_IR, mem_wb_1_alu_2,
       mem_wb_1_md_2, mips_alu_1_result, mips_regifile_1_r1, mips_regifile_1_r2, multiplexer_1_out,
       multiplexer_2_out, multiplexer_3_out, multiplexer_10_out, multiplexer_13_out, multiplexer_17_out,
       offset, PC_4, ram_1_data, shifter_1_out, WB_IR, \条件跳转 ;

  Button \u_总复位  (.out(RST));
  Button _1 (.out(IR1));
  Button _2 (.out(IR2));
  Button _3 (.out(IR3));
  // Probe on \总周期数 
  // Probe on \总周期数 
  Button \u_继续运行  (.out(Go));
  LED #(.active("true")) led_1 (.in(W1));
  LED #(.active("true")) led_2 (.in(W2));
  LED #(.active("true")) led_3 (.in(W3));
  Hex_Digit_Display hex_digit_display_1 (.value(LedData[31:28]));  // open: dp
  // Probe on IF_PC[19:0]
  // Mips_Probe mips_probe_1: pin names not known; wires that end beside it: IF_IR
  Hex_Digit_Display hex_digit_display_2 (.value(LedData[27:24]));  // open: dp
  Hex_Digit_Display hex_digit_display_3 (.value(LedData[23:20]));  // open: dp
  // Probe on ID_PC[19:0]
  // Mips_Probe mips_probe_2: pin names not known; wires that end beside it: ID_IR
  and and_1 (halt_t, Halt, 1'b0);
  Hex_Digit_Display hex_digit_display_4 (.value(LedData[19:16]));  // open: dp
  Hex_Digit_Display hex_digit_display_5 (.value(LedData[15:12]));  // open: dp
  or or_1 (IF_ID_flush, BranchBubble, RST);
  or or_2 (ID_EX_flush, DataHazzard, BranchBubble, RST);
  Hex_Digit_Display hex_digit_display_6 (.value(LedData[7:4]));  // open: dp
  Hex_Digit_Display hex_digit_display_7 (.value(LedData[11:8]));  // open: dp
  Clock #(.highDuration(1), .lowDuration(1)) clock_1 (.out(CLK));
  // Probe on EX_PC[19:0]
  // Mips_Probe mips_probe_3: pin names not known; wires that end beside it: EX_IR
  Multiplexer #(.select(1), .width(32), .disabled("Z"), .enable("false")) multiplexer_1 (
    .in0(PC_4), .in1(\条件跳转 ), .out(multiplexer_1_out), .sel(or_5_out));
  Multiplexer #(.select(1), .width(32), .disabled("Z"), .enable("false")) multiplexer_2 (
    .in0(multiplexer_1_out), .in1({EX_PC_4[31:28], \无条件跳转 , 2'b00}), .out(multiplexer_2_out),
    .sel(id_ex_1_jmp_2));
  Hex_Digit_Display hex_digit_display_8 (.value(LedData[3:0]));  // open: dp
  Multiplexer #(.select(1), .width(32), .disabled("Z"), .enable("false")) multiplexer_3 (
    .in0(multiplexer_2_out), .in1(JRPC), .out(multiplexer_3_out), .sel(id_ex_1_jr_2));
  // Probe on \总周期数 
  // Probe on M_PC[19:0]
  // Mips_Probe mips_probe_4: pin names not known; wires that end beside it: MEM_IR
  // Probe on \总周期数 
  // Probe on \无条件分支数 
  // Probe on \条件分支成功数 
  // Probe on \插入气泡数 
  // Probe on \LoadUse次数 
  Register #(.width(32), .trigger("rising"), .Select("low")) PC (
    .D(multiplexer_3_out), .en(PC_EN), .Q(IF_PC), .clk(CLK), .clr(RST));
  not not_1 (not_1_out, BranchBubble);
  not not_2 (not_2_out, BranchBubble);
  // Probe on IF_PC[11:0]
  // Probe on WB_PC[19:0]
  // Mips_Probe mips_probe_5: pin names not known; wires that end beside it: WB_IR
  Adder #(.width(32)) adder_1 (.a(IF_PC), .b(32'h4), .out(PC_4));  // open: cin, cout
  and and_2 (and_2_out, not_1_out, DataHazzard);
  and and_3 (and_3_out, not_2_out, DataHazzard);
  // Probe on EX_PC[11:0]
  // Probe on ID_PC[11:0]
  or or_3 (or_3_out, halt_t, and_2_out);
  not not_3 (PC_EN, or_3_out);
  or or_4 (IF_ID_EN, halt_t, and_3_out);
  // Probe on M_PC[11:0]
  D_Flip_Flop #(.trigger("high"), .Pre_Clr_Positions("LEGACY"), .NegatePresetClear("false"), .enable("true"), .NewFFLayout("false")) d_ff_1 (.Q(d_ff_1_q));  // open: clk, D, Qn, preset, en, reset
  // Probe on 13'hc
  ROM #(.addrWidth(10), .dataWidth(32), .Select("high")) rom_1 (.addr(IF_PC[11:2]), .data(IF_IR));
  // Probe on WB_PC[11:0]
  Comparator #(.width(13), .mode("twosComplement")) comparator_1 (
    .a(CNT_num), .b(13'hc), .eq(comparator_1_eq), .lt(comparator_1_lt));  // open: gt
  IF_ID if_id_1 (
    .CLK(CLK), .\同步清0_高电平有效 (IF_ID_flush), .\使能端_低电平有效 (IF_ID_EN), .PC(IF_PC), .IR(IF_IR), .PC_4(PC_4),
    .PC_2(ID_PC), .IR_2(ID_IR), .PC_4_2(if_id_1_pc_4_2));
  nand nand_1 (nand_1_out, d_ff_1_q, comparator_1_eq);
  Counter #(.width(13), .max('h1fff), .ongoal("stay"), .trigger("rising"), .behavior("old")) counter_1 (
    .count(comparator_1_lt), .Q(CNT_num), .clk(undriven));  // open: load, D, carry, clr, preset
  assign CLK = nand_1_out ? undriven : 1'bz;  // Controlled_Buffer controlled_buffer_1
  Pull_Resistor #(.pull(1)) pull_resistor_1 (.node(CLK));
  Button button_1 (.out(RST));
  not not_4 (not_4_out, halt_t);
  Counter #(.width(16), .max('hffff), .ongoal("wrap"), .trigger("rising"), .behavior("new")) counter_2 (
    .count(not_4_out), .Q(\总周期数 ), .clk(CLK), .clr(RST));  // open: load, D, carry, preset, down
  \单周期硬布线控制器  \u_单周期硬布线控制器_1  (
    .Func(ID_IR[5:0]), .OP(ID_IR[31:26]), .ALU_OP(\单周期硬布线控制器_1_alu_op ), .MemToReg(\单周期硬布线控制器_1_memtoreg ),
    .MemWrite(\单周期硬布线控制器_1_memwrite ), .ALU_SRC(\单周期硬布线控制器_1_alu_src ), .RegWrite(\单周期硬布线控制器_1_regwrite ),
    .SysCALL(\单周期硬布线控制器_1_syscall ), .SignedExt(\单周期硬布线控制器_1_signedext ), .RegDst(\单周期硬布线控制器_1_regdst ),
    .JR(\单周期硬布线控制器_1_jr ), .JMP(\单周期硬布线控制器_1_jmp ), .Beq(\单周期硬布线控制器_1_beq ), .JAL(\单周期硬布线控制器_1_jal ),
    .Bne(\单周期硬布线控制器_1_bne ), .SH(\单周期硬布线控制器_1_sh ), .BGTZ(\单周期硬布线控制器_1_bgtz ), .RtUsed(R2Used),
    .RsUsed(R1Used));  // open: LUI
  Multiplexer #(.select(1), .width(5), .disabled("Z"), .enable("false")) multiplexer_4 (
    .in0(WB_IR[20:16]), .in1(WB_IR[15:11]), .out(multiplexer_4_out), .sel(RegDst));
  Multiplexer #(.select(1), .width(5), .disabled("Z"), .enable("false")) multiplexer_5 (
    .in0(ID_IR[25:21]), .in1(5'b00010), .out(R1), .sel(\单周期硬布线控制器_1_syscall ));
  Multiplexer #(.select(1), .width(5), .disabled("Z"), .enable("false")) multiplexer_6 (
    .in0(ID_IR[20:16]), .in1(5'b00100), .out(R2), .sel(\单周期硬布线控制器_1_syscall ));
  Multiplexer #(.select(1), .width(5), .disabled("Z"), .enable("false")) multiplexer_7 (
    .in0(multiplexer_4_out), .in1({5{1'b1}}), .out(multiplexer_7_out), .sel(JAL));
  Multiplexer #(.select(1), .width(32), .disabled("Z"), .enable("false")) multiplexer_8 (
    .in0(multiplexer_17_out), .in1(JALPC), .out(RDin), .sel(JAL));
  // 数据冲突检测 数据冲突检测_1: pin names not known; wires that end beside it: R1Used, R2Used, R1, R2, EX_RegWrite, MEM_RegWrite, EX_WriteReg_num, MEM_WriteReg_num, DataHazzard
  MIPS_Regifile mips_regifile_1 (
    .Din(RDin), .Clk(CLK), .R1(mips_regifile_1_r1), .R2(mips_regifile_1_r2), .WE(RegWrite),
    .W_num(multiplexer_7_out), .R1_num(R1), .R2_num(R2));
  assign bit_extender_1_out = {{16{1'b0}}, \无条件跳转 [17:2]};  // Bit_Extender bit_extender_1
  assign bit_extender_2_out = {{16{\无条件跳转 [17]}}, \无条件跳转 [17:2]};  // Bit_Extender bit_extender_2
  Multiplexer #(.select(1), .width(32), .disabled("Z"), .enable("false")) multiplexer_9 (
    .in0(bit_extender_1_out), .in1(bit_extender_2_out), .out(offset), .sel(SignedExt));
  ID_EX id_ex_1 (
    .CLK(CLK), .\同步清0_高电平有效 (ID_EX_flush), .\使能端_低电平有效 (halt_t), .PC(ID_PC), .IR(ID_IR),
    .PC_4(if_id_1_pc_4_2), .R1(mips_regifile_1_r1), .R2(mips_regifile_1_r2), .Imm26(ID_IR[25:0]),
    .BGTZ(\单周期硬布线控制器_1_bgtz ), .BEQ(\单周期硬布线控制器_1_beq ), .BNE(\单周期硬布线控制器_1_bne ), .JR(\单周期硬布线控制器_1_jr ),
    .JMP(\单周期硬布线控制器_1_jmp ), .SignedExt(\单周期硬布线控制器_1_signedext ), .Syscall(\单周期硬布线控制器_1_syscall ),
    .MemToReg(\单周期硬布线控制器_1_memtoreg ), .RegWrite(\单周期硬布线控制器_1_regwrite ), .RegDst(\单周期硬布线控制器_1_regdst ),
    .JAL(\单周期硬布线控制器_1_jal ), .MemWrite(\单周期硬布线控制器_1_memwrite ), .SH(\单周期硬布线控制器_1_sh ),
    .AluSrcB(\单周期硬布线控制器_1_alu_src ), .AluOP(\单周期硬布线控制器_1_alu_op ), .PC_2(EX_PC), .IR_2(EX_IR),
    .PC_4_2(EX_PC_4), .R1_2(JRPC), .R2_2(id_ex_1_r2_2), .Imm26_2(\无条件跳转 ), .BGTZ_2(id_ex_1_bgtz_2),
    .BEQ_2(id_ex_1_beq_2), .BNE_2(id_ex_1_bne_2), .JR_2(id_ex_1_jr_2), .JMP_2(id_ex_1_jmp_2),
    .SignedExt_2(SignedExt), .Syscall_2(id_ex_1_syscall_2), .MemToReg_2(id_ex_1_memtoreg_2),
    .RegWrite_2(EX_RegWrite), .RegDst_2(id_ex_1_regdst_2), .JAL_2(id_ex_1_jal_2),
    .MemWrite_2(id_ex_1_memwrite_2), .SH_2(id_ex_1_sh_2), .AluSrcB_2(id_ex_1_alusrcb_2),
    .AluOP_2(id_ex_1_aluop_2));  // open: ForwardRs, ForwardRs_2, ForwardRt, ForwardRt_2, LUI, LUI_2
  Shifter #(.width(32), .shift("ll")) shifter_1 (.in(offset), .\dist (5'b00010), .out(shifter_1_out));
  Adder #(.width(32)) adder_2 (.a(shifter_1_out), .b(EX_PC_4), .out(\条件跳转 ));  // open: cin, cout
  Comparator #(.width(32), .mode("twosComplement")) comparator_2 (
    .a(JRPC), .b({32{1'b0}}), .gt(comparator_2_gt));  // open: eq, lt
  and and_4 (and_4_out, id_ex_1_bgtz_2, comparator_2_gt);
  Multiplexer #(.select(1), .width(32), .disabled("Z"), .enable("false")) multiplexer_10 (
    .in0(id_ex_1_r2_2), .in1(offset), .out(multiplexer_10_out), .sel(id_ex_1_alusrcb_2));
  and and_5 (and_5_out, id_ex_1_beq_2, mips_alu_1_equal);
  not not_5 (not_5_out, mips_alu_1_equal);
  MIPS_ALU mips_alu_1 (
    .X(JRPC), .Y(multiplexer_10_out), .AluOP(id_ex_1_aluop_2), .Equal(mips_alu_1_equal),
    .Result(mips_alu_1_result), .shamt(\无条件跳转 [12:8]));  // open: Result_2
  Register #(.width(32), .trigger("rising"), .Select("low")) register_1 (
    .D(id_ex_1_r2_2), .en(LED), .Q(LedData), .clk(CLK));  // open: clr
  and and_6 (and_6_out, id_ex_1_bne_2, not_5_out);
  or or_5 (or_5_out, and_4_out, and_5_out, and_6_out);
  or or_6 (BranchBubble, id_ex_1_jmp_2, id_ex_1_jr_2, or_5_out);
  Comparator #(.width(32), .mode("twosComplement")) comparator_3 (
    .a(JRPC), .b(32'h32), .eq(comparator_3_eq));  // open: gt, lt
  not not_6 (not_6_out, comparator_3_eq);
  Multiplexer #(.select(1), .width(5), .disabled("Z"), .enable("false")) multiplexer_11 (
    .in0(EX_IR[20:16]), .in1(EX_IR[15:11]), .out(multiplexer_11_out), .sel(id_ex_1_regdst_2));
  and and_7 (Halt, id_ex_1_syscall_2, comparator_3_eq);
  and and_8 (LED, id_ex_1_syscall_2, not_6_out);
  Multiplexer #(.select(1), .width(5), .disabled("Z"), .enable("false")) multiplexer_12 (
    .in0(multiplexer_11_out), .in1({5{1'b1}}), .out(EX_WriteReg_num), .sel(id_ex_1_jal_2));
  EX_MEM ex_mem_1 (
    .CLK(CLK), .\同步清0_高电平有效 (RST), .\使能端_低电平有效 (halt_t), .IR(EX_IR), .PC_4(EX_PC_4), .R2(id_ex_1_r2_2),
    .Alu(mips_alu_1_result), .Syscall(id_ex_1_syscall_2), .MemToReg(id_ex_1_memtoreg_2),
    .RegWrite(EX_RegWrite), .RegDst(id_ex_1_regdst_2), .JAL(id_ex_1_jal_2), .MemWrite(id_ex_1_memwrite_2),
    .SH(id_ex_1_sh_2), .PC_2(M_PC), .IR_2(MEM_IR), .PC_4_2(ex_mem_1_pc_4_2), .R2_2(ex_mem_1_r2_2),
    .Alu_2(ex_mem_1_alu_2), .Syscall_2(ex_mem_1_syscall_2), .MemToReg_2(ex_mem_1_memtoreg_2),
    .RegWrite_2(MEM_RegWrite), .RegDst_2(ex_mem_1_regdst_2), .JAL_2(ex_mem_1_jal_2), .MemWrite_2(MemWrite),
    .SH_2(ex_mem_1_sh_2), .PC(EX_PC));
  Multiplexer #(.select(1), .width(32), .disabled("Z"), .enable("false")) multiplexer_13 (
    .in0({ram_1_data[31:16], ex_mem_1_r2_2[15:0]}), .in1({ex_mem_1_r2_2[15:0], ram_1_data[15:0]}),
    .out(multiplexer_13_out), .sel(ex_mem_1_alu_2[1]));
  Multiplexer #(.select(1), .width(32), .disabled("Z"), .enable("false")) multiplexer_14 (
    .in0(ex_mem_1_r2_2), .in1(multiplexer_13_out), .out(MDin), .sel(ex_mem_1_sh_2));
  RAM #(.addrWidth(10), .dataWidth(32), .bus("separate"), .Select("high")) ram_1 (
    .addr(ex_mem_1_alu_2[11:2]), .din(MDin), .data(ram_1_data), .str(MemWrite), .clk(CLK), .clr(RST));  // open: sel, ld
  Multiplexer #(.select(1), .width(5), .disabled("Z"), .enable("false")) multiplexer_15 (
    .in0(MEM_IR[20:16]), .in1(MEM_IR[15:11]), .out(multiplexer_15_out), .sel(ex_mem_1_regdst_2));
  Multiplexer #(.select(1), .width(5), .disabled("Z"), .enable("false")) multiplexer_16 (
    .in0(multiplexer_15_out), .in1({5{1'b1}}), .out(MEM_WriteReg_num), .sel(ex_mem_1_jal_2));
  MEM_WB mem_wb_1 (
    .CLK(CLK), .\同步清0_高电平有效 (RST), .\使能端_低电平有效 (halt_t), .IR(MEM_IR), .PC_4(ex_mem_1_pc_4_2),
    .MD(ram_1_data), .Alu(ex_mem_1_alu_2), .Syscall(ex_mem_1_syscall_2), .MemToReg(ex_mem_1_memtoreg_2),
    .RegWrite(MEM_RegWrite), .RegDst(ex_mem_1_regdst_2), .JAL(ex_mem_1_jal_2), .PC_2(WB_PC), .IR_2(WB_IR),
    .PC_4_2(JALPC), .MD_2(mem_wb_1_md_2), .Alu_2(mem_wb_1_alu_2), .MemToReg_2(mem_wb_1_memtoreg_2),
    .RegWrite_2(RegWrite), .RegDst_2(RegDst), .JAL_2(JAL), .PC(M_PC));  // open: Syscall_2
  Multiplexer #(.select(1), .width(32), .disabled("Z"), .enable("false")) multiplexer_17 (
    .in0(mem_wb_1_alu_2), .in1(mem_wb_1_md_2), .out(multiplexer_17_out), .sel(mem_wb_1_memtoreg_2));

  // Other names for the same wires on the sheet: IR[31:0] = ID_IR; MEM_PC[31:0] = M_PC; PC[31:0] = IF_PC;
  //   WB_rd[4:0] = WB_IR[15:11]; WB_rt[4:0] = WB_IR[20:16]; 无条件跳转[31:28] = EX_PC_4[31:28]

  // Notes on the sheet:
  //   中断源
  //   时空图监测，可删除
  //   中断等待指示
  //   数码管输出
  //   控制位
  //   流水调试日志用
  //   暂停节拍，不能为0
  //   contents of rom_1 (hex, n*v repeats v):
  //   20110001 8000c05 20110001 20120002 20130003 8000c09 20110001 20120002 20130003 8000c0d 20110001
  //   20120002 20130003 8000c11 20110001 20120002 20130003 c000cb8 20100001 20110001 118fc0 112020
  //   20020022 c 118882 12200001 8000c15 112020 20020022 c 20110001 118880 112020 20020022 c 12200001
  //   8000c1f 20110001 118fc0 112020 20020022 c 1188c3 112020 20020022 c 118903 112020 20020022 c 118903
  //   112020 20020022 c 118903 112020 20020022 c 118903 112020 20020022 c 118903 112020 20020022 c 118903
  //   112020 20020022 c 118903 112020 20020022 c 20100001 109fc0 139fc3 8021 2012000c 24160003 26100001
  //   3210000f 20080008 20090001 139900 2709825 132020 20020022 c 1094022 1500fff9 22100001 2018000f
  //   2188024 108700 20080008 20090001 139902 2709825 132021 20020022 c 1094022 1500fff9 108702 2c9b022
  //   12c00001 8000c50 4020 1084027 84400 3508ffff 82021 20020022 c 2010ffff 20110000 ae300000 22100001
  //   22310004 ae300000 22100001 22310004 ae300000 22100001 22310004 ae300000 22100001 22310004 ae300000
  //   22100001 22310004 ae300000 22100001 22310004 ae300000 22100001 22310004 ae300000 22100001 22310004
  //   ae300000 22100001 22310004 ae300000 22100001 22310004 ae300000 22100001 22310004 ae300000 22100001
  //   22310004 ae300000 22100001 22310004 ae300000 22100001 22310004 ae300000 22100001 22310004 ae300000
  //   22100001 22310004 22100001 8020 2011003c 8e130000 8e340000 274402a 11000002 ae330000 ae140000
  //   2231fffc 1611fff8 102020 20020022 c 22100004 2011003c 1611fff2 20020032 c 20100000 22100001 102020
  //   20020022 c 22100002 102020 20020022 c 22100003 102020 20020022 c 22100004 102020 20020022 c 22100005
  //   102020 20020022 c 22100006 102020 20020022 c 22100007 102020 20020022 c 22100008 102020 20020022
  //   20020022 c 3e00008
  //   戳工具置1进入计数暂停模式，ctrl+k时钟自动运行到对应节拍暂停
  //   ctrl+k关闭时钟连续运行，将控制位置零，进入单步调试模式调试
  //   可计数暂停的时钟源
  //   指令存储器
  //   指令字
  //   OP
  //   Func
  //   rs
  //   rt
  //   imm26
  //   为方便自动评测，需要输出流水线各段保存的PC值，注意是PC不是PC+4，另外ID段寄存器写入信息，Mem段内存写入信息也要输出
  //   JMP
  //   JR
  //   OP
  //   Func
  //   Bne
  //   MemToReg
  //   MemWrite
  //   AluOP
  //   AluSrcB
  //   RegWrite
  //   JAL
  //   SH
  //   RegDst
  //   BGTZ
  //   Syscall
  //   rt
  //   rd
  //   rt
  //   rd
  //   rt
  //   rd
endmodule
module \重定向流水线  (
  output RegWrite,
  output MemWrite,
  output [31:0] IF_PC,
  output [31:0] ID_PC,
  output [31:0] EX_PC,
  output [31:0] M_PC,
  output [31:0] WB_PC,
  output [31:0] RDin,
  output [31:0] MDin,
  output [31:0] LedData
);

  wire and_2_out, and_3_out, and_4_out, and_5_out, and_6_out, BranchBubble, CLK, comparator_1_eq,
       comparator_1_lt, comparator_2_gt, comparator_3_eq, d_ff_1_q, DataHazzard, EX_LUI, ex_mem_1_jal_2,
       ex_mem_1_memtoreg_2, ex_mem_1_regdst_2, ex_mem_1_sh_2, ex_mem_1_syscall_2, EX_MemToReg, EX_RegWrite,
       Go, Halt, halt_t, id_ex_1_alusrcb_2, id_ex_1_beq_2, id_ex_1_bgtz_2, id_ex_1_bne_2, id_ex_1_jal_2,
       id_ex_1_jmp_2, id_ex_1_jr_2, id_ex_1_memwrite_2, id_ex_1_regdst_2, id_ex_1_sh_2, id_ex_1_syscall_2,
       ID_EX_flush, IF_ID_EN, IF_ID_flush, IR1, IR2, IR3, JAL, LED, LoadUse, MEM_RegWrite,
       mem_wb_1_memtoreg_2, mips_alu_1_equal, nand_1_out, not_1_out, not_2_out, not_4_out, not_5_out,
       not_6_out, or_3_out, or_5_out, PC_EN, R1Used, R2Used, RegDst, RST, SignedExt, undriven, W1, W2, W3,
       \单周期硬布线控制器_1_alu_src , \单周期硬布线控制器_1_beq , \单周期硬布线控制器_1_bgtz , \单周期硬布线控制器_1_bne , \单周期硬布线控制器_1_jal ,
       \单周期硬布线控制器_1_jmp , \单周期硬布线控制器_1_jr , \单周期硬布线控制器_1_lui , \单周期硬布线控制器_1_memtoreg ,
       \单周期硬布线控制器_1_memwrite , \单周期硬布线控制器_1_regdst , \单周期硬布线控制器_1_regwrite , \单周期硬布线控制器_1_sh ,
       \单周期硬布线控制器_1_signedext , \单周期硬布线控制器_1_syscall ;
  wire [1:0] EX_ForwardRs, EX_ForwardRt, ID_ForwardRs, ID_ForwardRt, \数据冲突检测_1_r1_ex_darahazarrd ,
       \数据冲突检测_1_r2_ex_darahazarrd ;
  wire [3:0] id_ex_1_aluop_2, \单周期硬布线控制器_1_alu_op ;
  wire [4:0] EX_WriteReg_num, MEM_WriteReg_num, multiplexer_4_out, multiplexer_7_out, multiplexer_12_out,
       multiplexer_14_out, multiplexer_20_out, R1, R2;
  wire [12:0] CNT_num;
  wire [15:0] \LoadUse次数 , ram_1_data, ram_1_data_2, \总周期数 , \插入气泡数 , \无条件分支数 , \条件分支成功数 ;
  wire [27:2] \无条件跳转 ;
  wire [31:0] bit_extender_1_out, bit_extender_2_out, EX_IR, ex_mem_1_pc_4_2, ex_mem_1_r2_2, EX_PC_4, EX_Rs,
       EX_Rt, ID_IR, if_id_1_pc_4_2, IF_IR, JALPC, JRPC, MEM_ALU, MEM_IR, mem_wb_1_alu_2, mem_wb_1_md_2,
       mips_alu_1_result, mips_regifile_1_r1, mips_regifile_1_r2, multiplexer_1_out, multiplexer_2_out,
       multiplexer_3_out, multiplexer_13_out, multiplexer_18_out, offset, PC_4, Rt_Redirect, shifter_1_out,
       WB_IR, WB_RES, \条件跳转 ;

  Button \u_总复位  (.out(RST));
  Button _1 (.out(IR1));
  Button _2 (.out(IR2));
  Button _3 (.out(IR3));
  // Probe on \总周期数 
  // Probe on \总周期数 
  Button \u_继续运行  (.out(Go));
  LED #(.active("true")) led_1 (.in(W1));
  LED #(.active("true")) led_2 (.in(W2));
  LED #(.active("true")) led_3 (.in(W3));
  Hex_Digit_Display hex_digit_display_1 (.value(LedData[31:28]));  // open: dp
  // Probe on IF_PC[19:0]
  // Mips_Probe mips_probe_1: pin names not known; wires that end beside it: IF_IR
  Hex_Digit_Display hex_digit_display_2 (.value(LedData[27:24]));  // open: dp
  Hex_Digit_Display hex_digit_display_3 (.value(LedData[23:20]));  // open: dp
  // Probe on ID_PC[19:0]
  // Mips_Probe mips_probe_2: pin names not known; wires that end beside it: ID_IR
  Hex_Digit_Display hex_digit_display_4 (.value(LedData[15:12]));  // open: dp
  Hex_Digit_Display hex_digit_display_5 (.value(LedData[19:16]));  // open: dp
  or or_1 (IF_ID_flush, BranchBubble, RST);
  or or_2 (ID_EX_flush, LoadUse, BranchBubble, RST);
  Hex_Digit_Display hex_digit_display_6 (.value(LedData[11:8]));  // open: dp
  Hex_Digit_Display hex_digit_display_7 (.value(LedData[7:4]));  // open: dp
  Clock #(.highDuration(1), .lowDuration(1)) clock_1 (.out(CLK));
  // Probe on EX_PC[19:0]
  // Mips_Probe mips_probe_3: pin names not known; wires that end beside it: EX_IR
  Multiplexer #(.select(1), .width(32), .disabled("Z"), .enable("false")) multiplexer_1 (
    .in0(PC_4), .in1(\条件跳转 ), .out(multiplexer_1_out), .sel(or_5_out));
  Hex_Digit_Display hex_digit_display_8 (.value(LedData[3:0]));  // open: dp
  Multiplexer #(.select(1), .width(32), .disabled("Z"), .enable("false")) multiplexer_2 (
    .in0(multiplexer_1_out), .in1({EX_PC_4[31:28], \无条件跳转 , 2'b00}), .out(multiplexer_2_out),
    .sel(id_ex_1_jmp_2));
  Multiplexer #(.select(1), .width(32), .disabled("Z"), .enable("false")) multiplexer_3 (
    .in0(multiplexer_2_out), .in1(JRPC), .out(multiplexer_3_out), .sel(id_ex_1_jr_2));
  // Probe on \总周期数 
  // Probe on M_PC[19:0]
  // Mips_Probe mips_probe_4: pin names not known; wires that end beside it: MEM_IR
  and and_1 (halt_t, Halt, 1'b0);
  // Probe on \总周期数 
  // Probe on \无条件分支数 
  // Probe on \条件分支成功数 
  // Probe on \插入气泡数 
  // Probe on \LoadUse次数 
  Register #(.width(32), .trigger("rising"), .Select("low")) PC (
    .D(multiplexer_3_out), .en(PC_EN), .Q(IF_PC), .clk(CLK), .clr(RST));
  not not_1 (not_1_out, BranchBubble);
  not not_2 (not_2_out, BranchBubble);
  // Probe on IF_PC[11:0]
  // Probe on WB_PC[19:0]
  // Mips_Probe mips_probe_5: pin names not known; wires that end beside it: WB_IR
  Adder #(.width(32)) adder_1 (.a(IF_PC), .b(32'h4), .out(PC_4));  // open: cin, cout
  and and_2 (and_2_out, not_1_out, LoadUse);
  and and_3 (and_3_out, not_2_out, LoadUse);
  // Probe on ID_PC[11:0]
  // Probe on EX_PC[11:0]
  or or_3 (or_3_out, halt_t, and_2_out);
  not not_3 (PC_EN, or_3_out);
  or or_4 (IF_ID_EN, halt_t, and_3_out);
  // Probe on M_PC[11:0]
  D_Flip_Flop #(.trigger("high"), .Pre_Clr_Positions("LEGACY"), .NegatePresetClear("false"), .enable("true"), .NewFFLayout("false")) d_ff_1 (.Q(d_ff_1_q));  // open: clk, D, Qn, preset, en, reset
  // Probe on 13'hc
  ROM #(.addrWidth(10), .dataWidth(32), .Select("high")) rom_1 (.addr(IF_PC[11:2]), .data(IF_IR));
  // Probe on WB_PC[11:0]
  Comparator #(.width(13), .mode("twosComplement")) comparator_1 (
    .a(CNT_num), .b(13'hc), .eq(comparator_1_eq), .lt(comparator_1_lt));  // open: gt
  nand nand_1 (nand_1_out, d_ff_1_q, comparator_1_eq);
  Counter #(.width(13), .max('h1fff), .ongoal("stay"), .trigger("rising"), .behavior("old")) counter_1 (
    .count(comparator_1_lt), .Q(CNT_num), .clk(undriven));  // open: load, D, carry, clr, preset
  IF_ID if_id_1 (
    .CLK(CLK), .\同步清0_高电平有效 (IF_ID_flush), .\使能端_低电平有效 (IF_ID_EN), .PC(IF_PC), .IR(IF_IR), .PC_4(PC_4),
    .PC_2(ID_PC), .IR_2(ID_IR), .PC_4_2(if_id_1_pc_4_2));
  assign CLK = nand_1_out ? undriven : 1'bz;  // Controlled_Buffer controlled_buffer_1
  Pull_Resistor #(.pull(1)) pull_resistor_1 (.node(CLK));
  Button button_1 (.out(RST));
  not not_4 (not_4_out, halt_t);
  Counter #(.width(16), .max('hffff), .ongoal("wrap"), .trigger("rising"), .behavior("new")) counter_2 (
    .count(not_4_out), .Q(\总周期数 ), .clk(CLK), .clr(RST));  // open: load, D, carry, preset, down
  \单周期硬布线控制器  \u_单周期硬布线控制器_1  (
    .Func(ID_IR[5:0]), .OP(ID_IR[31:26]), .ALU_OP(\单周期硬布线控制器_1_alu_op ), .MemToReg(\单周期硬布线控制器_1_memtoreg ),
    .MemWrite(\单周期硬布线控制器_1_memwrite ), .ALU_SRC(\单周期硬布线控制器_1_alu_src ), .RegWrite(\单周期硬布线控制器_1_regwrite ),
    .SysCALL(\单周期硬布线控制器_1_syscall ), .SignedExt(\单周期硬布线控制器_1_signedext ), .RegDst(\单周期硬布线控制器_1_regdst ),
    .JR(\单周期硬布线控制器_1_jr ), .JMP(\单周期硬布线控制器_1_jmp ), .Beq(\单周期硬布线控制器_1_beq ), .JAL(\单周期硬布线控制器_1_jal ),
    .Bne(\单周期硬布线控制器_1_bne ), .SH(\单周期硬布线控制器_1_sh ), .BGTZ(\单周期硬布线控制器_1_bgtz ), .RtUsed(R2Used),
    .RsUsed(R1Used), .LUI(\单周期硬布线控制器_1_lui ));
  Multiplexer #(.select(1), .width(5), .disabled("Z"), .enable("false")) multiplexer_4 (
    .in0(WB_IR[20:16]), .in1(WB_IR[15:11]), .out(multiplexer_4_out), .sel(RegDst));
  Multiplexer #(.select(1), .width(5), .disabled("Z"), .enable("false")) multiplexer_5 (
    .in0(ID_IR[25:21]), .in1(5'b00010), .out(R1), .sel(\单周期硬布线控制器_1_syscall ));
  Multiplexer #(.select(1), .width(5), .disabled("Z"), .enable("false")) multiplexer_6 (
    .in0(ID_IR[20:16]), .in1(5'b00100), .out(R2), .sel(\单周期硬布线控制器_1_syscall ));
  Multiplexer #(.select(1), .width(5), .disabled("Z"), .enable("false")) multiplexer_7 (
    .in0(multiplexer_4_out), .in1({5{1'b1}}), .out(multiplexer_7_out), .sel(JAL));
  Multiplexer #(.select(1), .width(32), .disabled("Z"), .enable("false")) multiplexer_8 (
    .in0(WB_RES), .in1(JALPC), .out(RDin), .sel(JAL));
  MIPS_Regifile mips_regifile_1 (
    .Din(RDin), .Clk(CLK), .R1(mips_regifile_1_r1), .R2(mips_regifile_1_r2), .WE(RegWrite),
    .W_num(multiplexer_7_out), .R1_num(R1), .R2_num(R2));
  assign bit_extender_1_out = {{16{1'b0}}, \无条件跳转 [17:2]};  // Bit_Extender bit_extender_1
  assign bit_extender_2_out = {{16{\无条件跳转 [17]}}, \无条件跳转 [17:2]};  // Bit_Extender bit_extender_2
  \数据冲突检测  \u_数据冲突检测_1  (
    .RsUsed(R1Used), .RtUsed(R2Used), .rs(R1), .rt(R2), .EX_RegWrite(EX_RegWrite),
    .MEM_RegWrite(MEM_RegWrite), .EX_WriteReg_num(EX_WriteReg_num), .MEM_WriteReg_num(MEM_WriteReg_num),
    .DataHazzard(DataHazzard), .LoadUse(LoadUse), .EX_MemToReg(EX_MemToReg),
    .R1_EX_DaraHazarrd(\数据冲突检测_1_r1_ex_darahazarrd [0]), .R2_EX_DaraHazarrd(\数据冲突检测_1_r2_ex_darahazarrd [0]),
    .R1_MEM_DaraHazarrd(\数据冲突检测_1_r1_ex_darahazarrd [1]), .R2_MEM_DaraHazarrd(\数据冲突检测_1_r2_ex_darahazarrd [1]));
  Multiplexer #(.select(1), .width(32), .disabled("Z"), .enable("false")) multiplexer_9 (
    .in0(bit_extender_1_out), .in1(bit_extender_2_out), .out(offset), .sel(SignedExt));
  ID_EX id_ex_1 (
    .CLK(CLK), .\同步清0_高电平有效 (ID_EX_flush), .\使能端_低电平有效 (halt_t), .PC(ID_PC), .IR(ID_IR),
    .PC_4(if_id_1_pc_4_2), .R1(mips_regifile_1_r1), .R2(mips_regifile_1_r2), .Imm26(ID_IR[25:0]),
    .BGTZ(\单周期硬布线控制器_1_bgtz ), .BEQ(\单周期硬布线控制器_1_beq ), .BNE(\单周期硬布线控制器_1_bne ), .JR(\单周期硬布线控制器_1_jr ),
    .JMP(\单周期硬布线控制器_1_jmp ), .SignedExt(\单周期硬布线控制器_1_signedext ), .Syscall(\单周期硬布线控制器_1_syscall ),
    .MemToReg(\单周期硬布线控制器_1_memtoreg ), .RegWrite(\单周期硬布线控制器_1_regwrite ), .RegDst(\单周期硬布线控制器_1_regdst ),
    .JAL(\单周期硬布线控制器_1_jal ), .MemWrite(\单周期硬布线控制器_1_memwrite ), .SH(\单周期硬布线控制器_1_sh ),
    .AluSrcB(\单周期硬布线控制器_1_alu_src ), .AluOP(\单周期硬布线控制器_1_alu_op ), .PC_2(EX_PC), .IR_2(EX_IR),
    .PC_4_2(EX_PC_4), .R1_2(EX_Rs), .R2_2(EX_Rt), .Imm26_2(\无条件跳转 ), .BGTZ_2(id_ex_1_bgtz_2),
    .BEQ_2(id_ex_1_beq_2), .BNE_2(id_ex_1_bne_2), .JR_2(id_ex_1_jr_2), .JMP_2(id_ex_1_jmp_2),
    .SignedExt_2(SignedExt), .Syscall_2(id_ex_1_syscall_2), .MemToReg_2(EX_MemToReg),
    .RegWrite_2(EX_RegWrite), .RegDst_2(id_ex_1_regdst_2), .JAL_2(id_ex_1_jal_2),
    .MemWrite_2(id_ex_1_memwrite_2), .SH_2(id_ex_1_sh_2), .AluSrcB_2(id_ex_1_alusrcb_2),
    .AluOP_2(id_ex_1_aluop_2), .ForwardRs(ID_ForwardRs), .ForwardRs_2(EX_ForwardRs),
    .ForwardRt(ID_ForwardRt), .ForwardRt_2(EX_ForwardRt), .LUI(\单周期硬布线控制器_1_lui ), .LUI_2(EX_LUI));
  Shifter #(.width(32), .shift("ll")) shifter_1 (.in(offset), .\dist (5'b00010), .out(shifter_1_out));
  Multiplexer #(.select(1), .width(2), .disabled("Z"), .enable("false")) multiplexer_10 (
    .in0(\数据冲突检测_1_r1_ex_darahazarrd ), .in1(2'b00), .out(ID_ForwardRs), .sel(LoadUse));
  Multiplexer #(.select(1), .width(2), .disabled("Z"), .enable("false")) multiplexer_11 (
    .in0(\数据冲突检测_1_r2_ex_darahazarrd ), .in1(2'b00), .out(ID_ForwardRt), .sel(LoadUse));
  Multiplexer #(.select(1), .width(5), .disabled("Z"), .enable("false")) multiplexer_12 (
    .in0(\无条件跳转 [12:8]), .in1(5'b10000), .out(multiplexer_12_out), .sel(EX_LUI));
  Adder #(.width(32)) adder_2 (.a(shifter_1_out), .b(EX_PC_4), .out(\条件跳转 ));  // open: cin, cout
  Comparator #(.width(32), .mode("twosComplement")) comparator_2 (
    .a(JRPC), .b({32{1'b0}}), .gt(comparator_2_gt));  // open: eq, lt
  Multiplexer #(.select(1), .width(32), .disabled("Z"), .enable("false")) multiplexer_13 (
    .in0(Rt_Redirect), .in1(offset), .out(multiplexer_13_out), .sel(id_ex_1_alusrcb_2));
  and and_4 (and_4_out, id_ex_1_bgtz_2, comparator_2_gt);
  and and_5 (and_5_out, id_ex_1_beq_2, mips_alu_1_equal);
  not not_5 (not_5_out, mips_alu_1_equal);
  MIPS_ALU mips_alu_1 (
    .X(JRPC), .Y(multiplexer_13_out), .AluOP(id_ex_1_aluop_2), .Equal(mips_alu_1_equal),
    .Result(mips_alu_1_result), .shamt(multiplexer_12_out));  // open: Result_2
  Register #(.width(32), .trigger("rising"), .Select("low")) register_1 (
    .D(Rt_Redirect), .en(LED), .Q(LedData), .clk(CLK));  // open: clr
  and and_6 (and_6_out, id_ex_1_bne_2, not_5_out);
  or or_5 (or_5_out, and_4_out, and_5_out, and_6_out);
  or or_6 (BranchBubble, id_ex_1_jmp_2, id_ex_1_jr_2, or_5_out);
  Comparator #(.width(32), .mode("twosComplement")) comparator_3 (
    .a(JRPC), .b(32'h32), .eq(comparator_3_eq));  // open: gt, lt
  not not_6 (not_6_out, comparator_3_eq);
  Multiplexer #(.select(1), .width(5), .disabled("Z"), .enable("false")) multiplexer_14 (
    .in0(EX_IR[20:16]), .in1(EX_IR[15:11]), .out(multiplexer_14_out), .sel(id_ex_1_regdst_2));
  and and_7 (Halt, id_ex_1_syscall_2, comparator_3_eq);
  and and_8 (LED, id_ex_1_syscall_2, not_6_out);
  Multiplexer #(.select(2), .width(32), .disabled("Z"), .enable("false")) multiplexer_15 (
    .in0(EX_Rs), .in1(MEM_ALU), .in2(WB_RES), .in3(MEM_ALU), .out(JRPC), .sel(EX_ForwardRs));
  Multiplexer #(.select(1), .width(5), .disabled("Z"), .enable("false")) multiplexer_16 (
    .in0(multiplexer_14_out), .in1({5{1'b1}}), .out(EX_WriteReg_num), .sel(id_ex_1_jal_2));
  EX_MEM ex_mem_1 (
    .CLK(CLK), .\同步清0_高电平有效 (RST), .\使能端_低电平有效 (halt_t), .IR(EX_IR), .PC_4(EX_PC_4), .R2(Rt_Redirect),
    .Alu(mips_alu_1_result), .Syscall(id_ex_1_syscall_2), .MemToReg(EX_MemToReg), .RegWrite(EX_RegWrite),
    .RegDst(id_ex_1_regdst_2), .JAL(id_ex_1_jal_2), .MemWrite(id_ex_1_memwrite_2), .SH(id_ex_1_sh_2),
    .PC_2(M_PC), .IR_2(MEM_IR), .PC_4_2(ex_mem_1_pc_4_2), .R2_2(ex_mem_1_r2_2), .Alu_2(MEM_ALU),
    .Syscall_2(ex_mem_1_syscall_2), .MemToReg_2(ex_mem_1_memtoreg_2), .RegWrite_2(MEM_RegWrite),
    .RegDst_2(ex_mem_1_regdst_2), .JAL_2(ex_mem_1_jal_2), .MemWrite_2(MemWrite), .SH_2(ex_mem_1_sh_2),
    .PC(EX_PC));
  Multiplexer #(.select(1), .width(32), .disabled("Z"), .enable("false")) multiplexer_17 (
    .in0(ex_mem_1_r2_2), .in1(multiplexer_18_out), .out(MDin), .sel(ex_mem_1_sh_2));
  Multiplexer #(.select(1), .width(32), .disabled("Z"), .enable("false")) multiplexer_18 (
    .in0({ram_1_data, ex_mem_1_r2_2[15:0]}), .in1({ex_mem_1_r2_2[15:0], ram_1_data_2}),
    .out(multiplexer_18_out), .sel(MEM_ALU[1]));
  Multiplexer #(.select(2), .width(32), .disabled("Z"), .enable("false")) multiplexer_19 (
    .in0(EX_Rt), .in1(MEM_ALU), .in2(WB_RES), .in3(MEM_ALU), .out(Rt_Redirect), .sel(EX_ForwardRt));
  RAM #(.addrWidth(10), .dataWidth(32), .bus("separate"), .Select("high")) ram_1 (
    .addr(MEM_ALU[11:2]), .din(MDin), .data({ram_1_data, ram_1_data_2}), .str(MemWrite), .clk(CLK), .clr(RST));  // open: sel, ld
  Multiplexer #(.select(1), .width(5), .disabled("Z"), .enable("false")) multiplexer_20 (
    .in0(MEM_IR[20:16]), .in1(MEM_IR[15:11]), .out(multiplexer_20_out), .sel(ex_mem_1_regdst_2));
  Multiplexer #(.select(1), .width(5), .disabled("Z"), .enable("false")) multiplexer_21 (
    .in0(multiplexer_20_out), .in1({5{1'b1}}), .out(MEM_WriteReg_num), .sel(ex_mem_1_jal_2));
  MEM_WB mem_wb_1 (
    .CLK(CLK), .\同步清0_高电平有效 (RST), .\使能端_低电平有效 (halt_t), .IR(MEM_IR), .PC_4(ex_mem_1_pc_4_2),
    .MD({ram_1_data, ram_1_data_2}), .Alu(MEM_ALU), .Syscall(ex_mem_1_syscall_2),
    .MemToReg(ex_mem_1_memtoreg_2), .RegWrite(MEM_RegWrite), .RegDst(ex_mem_1_regdst_2),
    .JAL(ex_mem_1_jal_2), .PC_2(WB_PC), .IR_2(WB_IR), .PC_4_2(JALPC), .MD_2(mem_wb_1_md_2),
    .Alu_2(mem_wb_1_alu_2), .MemToReg_2(mem_wb_1_memtoreg_2), .RegWrite_2(RegWrite), .RegDst_2(RegDst),
    .JAL_2(JAL), .PC(M_PC));  // open: Syscall_2
  Multiplexer #(.select(1), .width(32), .disabled("Z"), .enable("false")) multiplexer_22 (
    .in0(mem_wb_1_alu_2), .in1(mem_wb_1_md_2), .out(WB_RES), .sel(mem_wb_1_memtoreg_2));

  // Other names for the same wires on the sheet: IR[31:0] = ID_IR; MEM_PC[31:0] = M_PC; PC[31:0] = IF_PC;
  //   Rs_Redirect[31:0] = JRPC; WB_rd[4:0] = WB_IR[15:11]; WB_rt[4:0] = WB_IR[20:16]; 无条件跳转[31:28] = EX_PC_4[31:28]

  // Notes on the sheet:
  //   中断源
  //   中断等待指示
  //   数码管输出
  //   流水调试日志用
  //   控制位
  //   暂停节拍，不能为0
  //   contents of rom_1 (hex, n*v repeats v):
  //   2011000f 112020 20020022 c 2231ffff 1e20fffb 2002000a c
  //   戳工具置1进入计数暂停模式，ctrl+k时钟自动运行到对应节拍暂停
  //   ctrl+k关闭时钟连续运行，将控制位置零，进入单步调试模式调试
  //   可计数暂停的时钟源
  //   指令存储器
  //   指令字
  //   OP
  //   Func
  //   rs
  //   rt
  //   imm26
  //   为方便自动评测，需要输出流水线各段保存的PC值，注意是PC不是PC+4，另外ID段寄存器写入信息，Mem段内存写入信息也要输出
  //   JMP
  //   JR
  //   OP
  //   Func
  //   Bne
  //   MemToReg
  //   MemWrite
  //   AluOP
  //   AluSrcB
  //   RegWrite
  //   JAL
  //   SH
  //   RegDst
  //   BGTZ
  //   Syscall
  //   rt
  //   rd
  //   rt
  //   rd
  //   rt
  //   rd
endmodule

module \中断按键参考电路  (
  input  \同步清零信号 ,
  output \与中断屏蔽位与 
);

  wire \_1号中断_out , and_1_out, clock_1_out, d_ff_1_q, or_1_out, or_2_out;

  Clock #(.highDuration(1), .lowDuration(1)) clock_1 (.out(clock_1_out));
  Button \_1号中断  (.out(\_1号中断_out ));
  or or_1 (or_1_out, \与中断屏蔽位与 , d_ff_1_q);
  LED #(.active("true")) \_1号中断等待指示灯  (.in(or_1_out));
  D_Flip_Flop #(.trigger("rising"), .Pre_Clr_Positions("LEGACY"), .NegatePresetClear("false"), .enable("true"), .NewFFLayout("false")) d_ff_1 (
    .clk(\_1号中断_out ), .D(1'b1), .Q(d_ff_1_q), .reset(\与中断屏蔽位与 ));  // open: Qn, preset, en
  or or_2 (or_2_out, d_ff_1_q, \与中断屏蔽位与 );
  and and_1 (and_1_out, or_2_out, ~\同步清零信号 );  // AND_Gate
  D_Flip_Flop #(.trigger("rising"), .Pre_Clr_Positions("LEGACY"), .NegatePresetClear("false"), .enable("true"), .NewFFLayout("false")) IR1 (
    .clk(clock_1_out), .D(and_1_out), .Q(\与中断屏蔽位与 ));  // open: Qn, preset, en, reset
  \单周期硬布线控制器  \u_单周期硬布线控制器_1  ();  // open: Func, OP, ALU_OP, MemToReg, MemWrite, ALU_SRC, RegWrite, SysCALL, SignedExt, RegDst, JR, JMP, Beq, JAL, Bne, SH, BGTZ, RtUsed, RsUsed, LUI

  // Notes on the sheet:
  //   中断信号采样参考电路
  //   Reset 
endmodule

module \单周期MIPS_单级中断  (
  input  IR1,
  input  IR2,
  input  IR3,
  output RegWrite,
  output MemWrite,
  output [31:0] PC,
  output [31:0] IR,
  output [31:0] RDin,
  output [31:0] MDin,
  output [31:0] LedData
);

  wire CLK, comparator_1_eq, comparator_2_eq, comparator_3_eq, comparator_4_eq, Go, IR1_t, IR2_t, IR3_t, IRA,
       IRB, IRC, or_1_out, W1, W2, W3;
  wire [15:0] \总周期数 ;

  Clock #(.highDuration(1), .lowDuration(1)) clock_1 (.out(CLK));
  Button _1 ();  // open: out
  Button _2 ();  // open: out
  Button _3 ();  // open: out
  Button \u_继续运行  (.out(Go));
  LED #(.active("true")) led_1 (.in(W1));
  LED #(.active("true")) led_2 (.in(W2));
  LED #(.active("true")) led_3 (.in(W3));
  Hex_Digit_Display hex_digit_display_1 (.value(LedData[31:28]));  // open: dp
  Comparator #(.width(16), .mode("twosComplement")) comparator_1 (
    .a(16'h23b), .b(\总周期数 ), .eq(comparator_1_eq));  // open: gt, lt
  Comparator #(.width(16), .mode("twosComplement")) comparator_2 (
    .a(\总周期数 ), .b(16'h1), .eq(comparator_2_eq));  // open: gt, lt
  Comparator #(.width(16), .mode("twosComplement")) comparator_3 (
    .a(\总周期数 ), .b(16'h4), .eq(comparator_3_eq));  // open: gt, lt
  Comparator #(.width(16), .mode("twosComplement")) comparator_4 (
    .a(\总周期数 ), .b(16'h7), .eq(comparator_4_eq));  // open: gt, lt
  Hex_Digit_Display hex_digit_display_2 (.value(LedData[27:24]));  // open: dp
  Hex_Digit_Display hex_digit_display_3 (.value(LedData[23:20]));  // open: dp
  or or_1 (or_1_out, comparator_1_eq, comparator_2_eq);
  assign IRA = or_1_out ? ~CLK : 1'bz;  // Controlled_Inverter controlled_inverter_1
  assign IRB = comparator_3_eq ? ~CLK : 1'bz;  // Controlled_Inverter controlled_inverter_2
  assign IRC = comparator_4_eq ? ~CLK : 1'bz;  // Controlled_Inverter controlled_inverter_3
  Hex_Digit_Display hex_digit_display_4 (.value(LedData[15:12]));  // open: dp
  Hex_Digit_Display hex_digit_display_5 (.value(LedData[19:16]));  // open: dp
  Pull_Resistor #(.pull(0)) pull_resistor_1 (.node(IRA));
  Pull_Resistor #(.pull(0)) pull_resistor_2 (.node(IRB));
  Pull_Resistor #(.pull(0)) pull_resistor_3 (.node(IRC));
  Hex_Digit_Display hex_digit_display_6 (.value(LedData[11:8]));  // open: dp
  Hex_Digit_Display hex_digit_display_7 (.value(LedData[7:4]));  // open: dp
  // Probe on \总周期数 
  Hex_Digit_Display hex_digit_display_8 (.value(LedData[3:0]));  // open: dp
  or or_2 (IR1_t, IR1, IRA);
  or or_3 (IR2_t, IR2, IRB);
  or or_4 (IR3_t, IR3, IRC);

  // Notes on the sheet:
  //   中断源
  //   中断等待指示
  //   总复位信号应将除ROM以外所有存储组件全部清零
  //   单级中断测试信号模拟器
  //   数码管输出
  //   数码管输出应该用寄存器锁存，否则显示数据只能一闪而过
  //   为方便自动评测，需要输出PC，IR，寄存器堆写如数据RDin
  //   RAM写使能MemWrite、RAM写入数据MDin等信号
endmodule

module \单周期MIPS_多级中断  (
  input  IR1,
  input  IR2,
  input  IR3,
  output RegWrite,
  output MemWrite,
  output [31:0] PC,
  output [31:0] IR,
  output [31:0] RDin,
  output [31:0] MDin,
  output [31:0] LedData
);

  wire CLK, comparator_1_eq, comparator_2_eq, comparator_3_eq, comparator_4_eq, comparator_5_eq, Go, IR1_t,
       IR2_t, IR3_t, IRA, IRB, IRC, or_1_out, or_2_out, W1, W2, W3;
  wire [15:0] \总周期数 ;

  Clock #(.highDuration(1), .lowDuration(1)) clock_1 (.out(CLK));
  Button _1 ();  // open: out
  Button _2 ();  // open: out
  Button _3 ();  // open: out
  Button \u_继续运行  (.out(Go));
  LED #(.active("true")) led_1 (.in(W1));
  LED #(.active("true")) led_2 (.in(W2));
  LED #(.active("true")) led_3 (.in(W3));
  Hex_Digit_Display hex_digit_display_1 (.value(LedData[31:28]));  // open: dp
  Comparator #(.width(16), .mode("twosComplement")) comparator_1 (
    .a(\总周期数 ), .b(16'h7), .eq(comparator_1_eq));  // open: gt, lt
  Comparator #(.width(16), .mode("twosComplement")) comparator_2 (
    .a(\总周期数 ), .b(16'h241), .eq(comparator_2_eq));  // open: gt, lt
  Hex_Digit_Display hex_digit_display_2 (.value(LedData[23:20]));  // open: dp
  Hex_Digit_Display hex_digit_display_3 (.value(LedData[27:24]));  // open: dp
  Comparator #(.width(16), .mode("twosComplement")) comparator_3 (
    .a(16'h258), .b(\总周期数 ), .eq(comparator_3_eq));  // open: gt, lt
  or or_1 (or_1_out, comparator_3_eq, comparator_4_eq);
  Comparator #(.width(16), .mode("twosComplement")) comparator_4 (
    .a(\总周期数 ), .b(16'h1), .eq(comparator_4_eq));  // open: gt, lt
  Comparator #(.width(16), .mode("twosComplement")) comparator_5 (
    .a(\总周期数 ), .b(16'h4), .eq(comparator_5_eq));  // open: gt, lt
  or or_2 (or_2_out, comparator_1_eq, comparator_2_eq);
  Hex_Digit_Display hex_digit_display_4 (.value(LedData[19:16]));  // open: dp
  Hex_Digit_Display hex_digit_display_5 (.value(LedData[15:12]));  // open: dp
  Pull_Resistor #(.pull(0)) pull_resistor_1 (.node(IRA));
  assign IRA = or_1_out ? ~CLK : 1'bz;  // Controlled_Inverter controlled_inverter_1
  Pull_Resistor #(.pull(0)) pull_resistor_2 (.node(IRB));
  assign IRB = comparator_5_eq ? ~CLK : 1'bz;  // Controlled_Inverter controlled_inverter_2
  Pull_Resistor #(.pull(0)) pull_resistor_3 (.node(IRC));
  assign IRC = or_2_out ? ~CLK : 1'bz;  // Controlled_Inverter controlled_inverter_3
  Hex_Digit_Display hex_digit_display_6 (.value(LedData[11:8]));  // open: dp
  Hex_Digit_Display hex_digit_display_7 (.value(LedData[7:4]));  // open: dp
  // Probe on \总周期数 
  Hex_Digit_Display hex_digit_display_8 (.value(LedData[3:0]));  // open: dp
  or or_3 (IR1_t, IR1, IRA);
  or or_4 (IR2_t, IR2, IRB);
  or or_5 (IR3_t, IR3, IRC);

  // Notes on the sheet:
  //   中断源
  //   中断等待指示
  //   总复位信号应将除ROM以外所有存储组件全部清零
  //   多级中断测试信号模拟器
  //   数码管输出
  //   数码管输出应该用寄存器锁存，否则显示数据只能一闪而过
  //   为方便自动评测，需要输出PC，IR，寄存器堆写如数据RDin
  //   RAM写使能MemWrite、RAM写入数据MDin等信号
endmodule

module \封装正确性测试  (
);

  wire IR1, IR2, IR3, MemW, RegW;
  wire [31:0] EX_PC, ID_PC, IF_PC, IR, LED, MDin, MDinr, MEM_PC, PC, RDin, RDinr, WB_PC;

  \单周期MIPS  \u_单周期mips_1  (
    .IR1(IR1), .IR2(IR2), .IR3(IR3), .RegWrite(RegW), .MemWrite(MemW), .PC(PC), .IR(IR), .RDin(RDin),
    .MDin(MDin), .LedData(LED));
  \气泡流水线  \u_气泡流水线_1  (
    .RegWrite(RegW), .MemWrite(MemW), .IF_PC(IF_PC), .ID_PC(ID_PC), .EX_PC(EX_PC), .M_PC(MEM_PC),
    .WB_PC(WB_PC), .RDin(RDinr), .MDin(MDinr), .LedData(LED));
  \单周期MIPS_单级中断  \u_单周期mips_单级中断_1  (
    .IR1(IR1), .IR2(IR2), .IR3(IR3), .RegWrite(RegW), .MemWrite(MemW), .PC(PC), .IR(IR), .RDin(RDin),
    .MDin(MDin), .LedData(LED));
  \理想流水线  \u_理想流水线_1  (
    .RegWrite(RegW), .MemWrite(MemW), .IF_PC(IF_PC), .ID_PC(ID_PC), .EX_PC(EX_PC), .M_PC(MEM_PC),
    .WB_PC(WB_PC), .RDin(RDinr), .MDin(MDinr), .LedData(LED));
  \重定向流水线  \u_重定向流水线_1  (
    .RegWrite(RegW), .MemWrite(MemW), .IF_PC(IF_PC), .ID_PC(ID_PC), .EX_PC(EX_PC), .M_PC(MEM_PC),
    .WB_PC(WB_PC), .RDin(RDinr), .MDin(MDinr), .LedData(LED));
  \单周期MIPS_多级中断  \u_单周期mips_多级中断_1  (
    .IR1(IR1), .IR2(IR2), .IR3(IR3), .RegWrite(RegW), .MemWrite(MemW), .PC(PC), .IR(IR), .RDin(RDin),
    .MDin(MDin), .LedData(LED));

  // Notes on the sheet:
  //   单周期封装测试
  //   气泡流水封装测试
  //   单周期+单级中断封装测试
  //   请检查上面封装有无位宽不匹配，引脚标签是否和连接的标签相对应，否则无法在educoder平台上正确测试
  //   理想流水封装测试
  //   重定向流水封装测试
  //   单周期+多级中断封装测试
endmodule

module IF_ID (
  input  CLK,
  input  \同步清0_高电平有效 ,
  input  \使能端_低电平有效 ,
  input  [31:0] PC,
  input  [31:0] IR,
  input  [31:0] PC_4,
  output [31:0] PC_2,
  output [31:0] IR_2,
  output [31:0] PC_4_2
);

  wire not_1_out;
  wire [31:0] multiplexer_1_out, multiplexer_2_out, multiplexer_3_out;

  Multiplexer #(.select(1), .width(32), .disabled("Z"), .enable("false")) multiplexer_1 (
    .in0(PC), .in1({32{1'b0}}), .out(multiplexer_1_out), .sel(\同步清0_高电平有效 ));
  Multiplexer #(.select(1), .width(32), .disabled("Z"), .enable("false")) multiplexer_2 (
    .in0(IR), .in1({32{1'b0}}), .out(multiplexer_2_out), .sel(\同步清0_高电平有效 ));
  Multiplexer #(.select(1), .width(32), .disabled("Z"), .enable("false")) multiplexer_3 (
    .in0(PC_4), .in1({32{1'b0}}), .out(multiplexer_3_out), .sel(\同步清0_高电平有效 ));
  not not_1 (not_1_out, \使能端_低电平有效 );
  Register #(.width(32), .trigger("rising"), .Select("low")) register_1 (
    .D(multiplexer_1_out), .en(not_1_out), .Q(PC_2), .clk(CLK));  // open: clr
  Register #(.width(32), .trigger("rising"), .Select("low")) register_2 (
    .D(multiplexer_2_out), .en(not_1_out), .Q(IR_2), .clk(CLK));  // open: clr
  Register #(.width(32), .trigger("rising"), .Select("low")) register_3 (
    .D(multiplexer_3_out), .en(not_1_out), .Q(PC_4_2), .clk(CLK));  // open: clr
  Pull_Resistor #(.pull(0)) pull_resistor_1 (.node(\同步清0_高电平有效 ));
  Pull_Resistor #(.pull(0)) pull_resistor_2 (.node(not_1_out));
endmodule

module ID_EX (
  input  CLK,
  input  \同步清0_高电平有效 ,
  input  \使能端_低电平有效 ,
  input  [31:0] PC,
  input  [31:0] IR,
  input  [31:0] PC_4,
  input  [31:0] R1,
  input  [31:0] R2,
  input  [25:0] Imm26,
  input  BGTZ,
  input  BEQ,
  input  BNE,
  input  JR,
  input  JMP,
  input  SignedExt,
  input  Syscall,
  input  MemToReg,
  input  RegWrite,
  input  RegDst,
  input  JAL,
  input  MemWrite,
  input  SH,
  input  AluSrcB,
  input  [3:0] AluOP,
  input  [1:0] ForwardRs,
  input  [1:0] ForwardRt,
  input  LUI,
  output [31:0] PC_2,
  output [31:0] IR_2,
  output [31:0] PC_4_2,
  output [31:0] R1_2,
  output [31:0] R2_2,
  output [25:0] Imm26_2,
  output BGTZ_2,
  output BEQ_2,
  output BNE_2,
  output JR_2,
  output JMP_2,
  output SignedExt_2,
  output Syscall_2,
  output MemToReg_2,
  output RegWrite_2,
  output RegDst_2,
  output JAL_2,
  output MemWrite_2,
  output SH_2,
  output AluSrcB_2,
  output [3:0] AluOP_2,
  output [1:0] ForwardRs_2,
  output [1:0] ForwardRt_2,
  output LUI_2
);

  wire multiplexer_3_out, multiplexer_4_out, multiplexer_5_out, multiplexer_6_out, multiplexer_7_out,
       multiplexer_8_out, multiplexer_9_out, multiplexer_10_out, multiplexer_11_out, multiplexer_12_out,
       multiplexer_13_out, multiplexer_14_out, multiplexer_15_out, multiplexer_16_out, multiplexer_20_out,
       not_1_out;
  wire [1:0] multiplexer_18_out, multiplexer_19_out;
  wire [3:0] multiplexer_17_out;
  wire [25:0] multiplexer_24_out;
  wire [31:0] multiplexer_1_out, multiplexer_2_out, multiplexer_21_out, multiplexer_22_out,
       multiplexer_23_out;

  Multiplexer #(.select(1), .width(32), .disabled("Z"), .enable("false")) multiplexer_1 (
    .in0(PC), .in1({32{1'b0}}), .out(multiplexer_1_out), .sel(\同步清0_高电平有效 ));
  Multiplexer #(.select(1), .width(32), .disabled("Z"), .enable("false")) multiplexer_2 (
    .in0(R1), .in1({32{1'b0}}), .out(multiplexer_2_out), .sel(\同步清0_高电平有效 ));
  Multiplexer #(.select(1), .width(1), .disabled("Z"), .enable("false")) multiplexer_3 (
    .in0(BGTZ), .in1(1'b0), .out(multiplexer_3_out), .sel(\同步清0_高电平有效 ));
  Multiplexer #(.select(1), .width(1), .disabled("Z"), .enable("false")) multiplexer_4 (
    .in0(BEQ), .in1(1'b0), .out(multiplexer_4_out), .sel(\同步清0_高电平有效 ));
  Multiplexer #(.select(1), .width(1), .disabled("Z"), .enable("false")) multiplexer_5 (
    .in0(BNE), .in1(1'b0), .out(multiplexer_5_out), .sel(\同步清0_高电平有效 ));
  Multiplexer #(.select(1), .width(1), .disabled("Z"), .enable("false")) multiplexer_6 (
    .in0(JR), .in1(1'b0), .out(multiplexer_6_out), .sel(\同步清0_高电平有效 ));
  Multiplexer #(.select(1), .width(1), .disabled("Z"), .enable("false")) multiplexer_7 (
    .in0(JMP), .in1(1'b0), .out(multiplexer_7_out), .sel(\同步清0_高电平有效 ));
  Multiplexer #(.select(1), .width(1), .disabled("Z"), .enable("false")) multiplexer_8 (
    .in0(SignedExt), .in1(1'b0), .out(multiplexer_8_out), .sel(\同步清0_高电平有效 ));
  Multiplexer #(.select(1), .width(1), .disabled("Z"), .enable("false")) multiplexer_9 (
    .in0(Syscall), .in1(1'b0), .out(multiplexer_9_out), .sel(\同步清0_高电平有效 ));
  Multiplexer #(.select(1), .width(1), .disabled("Z"), .enable("false")) multiplexer_10 (
    .in0(MemToReg), .in1(1'b0), .out(multiplexer_10_out), .sel(\同步清0_高电平有效 ));
  Multiplexer #(.select(1), .width(1), .disabled("Z"), .enable("false")) multiplexer_11 (
    .in0(RegWrite), .in1(1'b0), .out(multiplexer_11_out), .sel(\同步清0_高电平有效 ));
  Multiplexer #(.select(1), .width(1), .disabled("Z"), .enable("false")) multiplexer_12 (
    .in0(RegDst), .in1(1'b0), .out(multiplexer_12_out), .sel(\同步清0_高电平有效 ));
  Multiplexer #(.select(1), .width(1), .disabled("Z"), .enable("false")) multiplexer_13 (
    .in0(JAL), .in1(1'b0), .out(multiplexer_13_out), .sel(\同步清0_高电平有效 ));
  Multiplexer #(.select(1), .width(1), .disabled("Z"), .enable("false")) multiplexer_14 (
    .in0(MemWrite), .in1(1'b0), .out(multiplexer_14_out), .sel(\同步清0_高电平有效 ));
  Multiplexer #(.select(1), .width(1), .disabled("Z"), .enable("false")) multiplexer_15 (
    .in0(SH), .in1(1'b0), .out(multiplexer_15_out), .sel(\同步清0_高电平有效 ));
  Multiplexer #(.select(1), .width(1), .disabled("Z"), .enable("false")) multiplexer_16 (
    .in0(AluSrcB), .in1(1'b0), .out(multiplexer_16_out), .sel(\同步清0_高电平有效 ));
  Multiplexer #(.select(1), .width(4), .disabled("Z"), .enable("false")) multiplexer_17 (
    .in0(AluOP), .in1(4'b0000), .out(multiplexer_17_out), .sel(\同步清0_高电平有效 ));
  Multiplexer #(.select(1), .width(2), .disabled("Z"), .enable("false")) multiplexer_18 (
    .in0(ForwardRs), .in1(2'b00), .out(multiplexer_18_out), .sel(\同步清0_高电平有效 ));
  Multiplexer #(.select(1), .width(2), .disabled("Z"), .enable("false")) multiplexer_19 (
    .in0(ForwardRt), .in1(2'b00), .out(multiplexer_19_out), .sel(\同步清0_高电平有效 ));
  Multiplexer #(.select(1), .width(1), .disabled("Z"), .enable("false")) multiplexer_20 (
    .in0(LUI), .in1(1'b0), .out(multiplexer_20_out), .sel(\同步清0_高电平有效 ));
  Multiplexer #(.select(1), .width(32), .disabled("Z"), .enable("false")) multiplexer_21 (
    .in0(IR), .in1({32{1'b0}}), .out(multiplexer_21_out), .sel(\同步清0_高电平有效 ));
  Multiplexer #(.select(1), .width(32), .disabled("Z"), .enable("false")) multiplexer_22 (
    .in0(PC_4), .in1({32{1'b0}}), .out(multiplexer_22_out), .sel(\同步清0_高电平有效 ));
  Multiplexer #(.select(1), .width(32), .disabled("Z"), .enable("false")) multiplexer_23 (
    .in0(R2), .in1({32{1'b0}}), .out(multiplexer_23_out), .sel(\同步清0_高电平有效 ));
  Multiplexer #(.select(1), .width(26), .disabled("Z"), .enable("false")) multiplexer_24 (
    .in0(Imm26), .in1({26{1'b0}}), .out(multiplexer_24_out), .sel(\同步清0_高电平有效 ));
  not not_1 (not_1_out, \使能端_低电平有效 );
  Register #(.width(32), .trigger("rising"), .Select("low")) register_1 (
    .D(multiplexer_1_out), .en(not_1_out), .Q(PC_2), .clk(CLK));  // open: clr
  Register #(.width(32), .trigger("rising"), .Select("low")) register_2 (
    .D(multiplexer_21_out), .en(not_1_out), .Q(IR_2), .clk(CLK));  // open: clr
  Register #(.width(32), .trigger("rising"), .Select("low")) register_3 (
    .D(multiplexer_22_out), .en(not_1_out), .Q(PC_4_2), .clk(CLK));  // open: clr
  Register #(.width(32), .trigger("rising"), .Select("low")) register_4 (
    .D(multiplexer_2_out), .en(not_1_out), .Q(R1_2), .clk(CLK));  // open: clr
  Register #(.width(32), .trigger("rising"), .Select("low")) register_5 (
    .D(multiplexer_23_out), .en(not_1_out), .Q(R2_2), .clk(CLK));  // open: clr
  Register #(.width(26), .trigger("rising"), .Select("low")) register_6 (
    .D(multiplexer_24_out), .en(not_1_out), .Q(Imm26_2), .clk(CLK));  // open: clr
  Register #(.width(1), .trigger("rising"), .Select("low")) register_7 (
    .D(multiplexer_3_out), .en(not_1_out), .Q(BGTZ_2), .clk(CLK));  // open: clr
  Register #(.width(1), .trigger("rising"), .Select("low")) register_8 (
    .D(multiplexer_4_out), .en(not_1_out), .Q(BEQ_2), .clk(CLK));  // open: clr
  Register #(.width(1), .trigger("rising"), .Select("low")) register_9 (
    .D(multiplexer_5_out), .en(not_1_out), .Q(BNE_2), .clk(CLK));  // open: clr
  Register #(.width(1), .trigger("rising"), .Select("low")) register_10 (
    .D(multiplexer_6_out), .en(not_1_out), .Q(JR_2), .clk(CLK));  // open: clr
  Register #(.width(1), .trigger("rising"), .Select("low")) register_11 (
    .D(multiplexer_7_out), .en(not_1_out), .Q(JMP_2), .clk(CLK));  // open: clr
  Register #(.width(1), .trigger("rising"), .Select("low")) register_12 (
    .D(multiplexer_8_out), .en(not_1_out), .Q(SignedExt_2), .clk(CLK));  // open: clr
  Register #(.width(1), .trigger("rising"), .Select("low")) register_13 (
    .D(multiplexer_9_out), .en(not_1_out), .Q(Syscall_2), .clk(CLK));  // open: clr
  Register #(.width(1), .trigger("rising"), .Select("low")) register_14 (
    .D(multiplexer_10_out), .en(not_1_out), .Q(MemToReg_2), .clk(CLK));  // open: clr
  Register #(.width(1), .trigger("rising"), .Select("low")) register_15 (
    .D(multiplexer_11_out), .en(not_1_out), .Q(RegWrite_2), .clk(CLK));  // open: clr
  Register #(.width(1), .trigger("rising"), .Select("low")) register_16 (
    .D(multiplexer_12_out), .en(not_1_out), .Q(RegDst_2), .clk(CLK));  // open: clr
  Register #(.width(1), .trigger("rising"), .Select("low")) register_17 (
    .D(multiplexer_13_out), .en(not_1_out), .Q(JAL_2), .clk(CLK));  // open: clr
  Register #(.width(1), .trigger("rising"), .Select("low")) register_18 (
    .D(multiplexer_14_out), .en(not_1_out), .Q(MemWrite_2), .clk(CLK));  // open: clr
  Register #(.width(1), .trigger("rising"), .Select("low")) register_19 (
    .D(multiplexer_15_out), .en(not_1_out), .Q(SH_2), .clk(CLK));  // open: clr
  Register #(.width(1), .trigger("rising"), .Select("low")) register_20 (
    .D(multiplexer_16_out), .en(not_1_out), .Q(AluSrcB_2), .clk(CLK));  // open: clr
  Register #(.width(4), .trigger("rising"), .Select("low")) register_21 (
    .D(multiplexer_17_out), .en(not_1_out), .Q(AluOP_2), .clk(CLK));  // open: clr
  Register #(.width(2), .trigger("rising"), .Select("low")) register_22 (
    .D(multiplexer_18_out), .en(not_1_out), .Q(ForwardRs_2), .clk(CLK));  // open: clr
  Register #(.width(2), .trigger("rising"), .Select("low")) register_23 (
    .D(multiplexer_19_out), .en(not_1_out), .Q(ForwardRt_2), .clk(CLK));  // open: clr
  Register #(.width(1), .trigger("rising"), .Select("low")) register_24 (
    .D(multiplexer_20_out), .en(not_1_out), .Q(LUI_2), .clk(CLK));  // open: clr
  Pull_Resistor #(.pull(0)) pull_resistor_1 (.node(\同步清0_高电平有效 ));
  Pull_Resistor #(.pull(0)) pull_resistor_2 (.node(not_1_out));
endmodule

module EX_MEM (
  input  CLK,
  input  \同步清0_高电平有效 ,
  input  \使能端_低电平有效 ,
  input  [31:0] PC,
  input  [31:0] IR,
  input  [31:0] PC_4,
  input  [31:0] R2,
  input  [31:0] Alu,
  input  Syscall,
  input  MemToReg,
  input  RegWrite,
  input  RegDst,
  input  JAL,
  input  MemWrite,
  input  SH,
  output [31:0] PC_2,
  output [31:0] IR_2,
  output [31:0] PC_4_2,
  output [31:0] R2_2,
  output [31:0] Alu_2,
  output Syscall_2,
  output MemToReg_2,
  output RegWrite_2,
  output RegDst_2,
  output JAL_2,
  output MemWrite_2,
  output SH_2
);

  wire multiplexer_2_out, multiplexer_3_out, multiplexer_4_out, multiplexer_5_out, multiplexer_6_out,
       multiplexer_7_out, multiplexer_8_out, not_1_out;
  wire [31:0] multiplexer_1_out, multiplexer_9_out, multiplexer_10_out, multiplexer_11_out,
       multiplexer_12_out;

  Multiplexer #(.select(1), .width(32), .disabled("Z"), .enable("false")) multiplexer_1 (
    .in0(PC), .in1({32{1'b0}}), .out(multiplexer_1_out), .sel(\同步清0_高电平有效 ));
  Multiplexer #(.select(1), .width(1), .disabled("Z"), .enable("false")) multiplexer_2 (
    .in0(Syscall), .in1(1'b0), .out(multiplexer_2_out), .sel(\同步清0_高电平有效 ));
  Multiplexer #(.select(1), .width(1), .disabled("Z"), .enable("false")) multiplexer_3 (
    .in0(MemToReg), .in1(1'b0), .out(multiplexer_3_out), .sel(\同步清0_高电平有效 ));
  Multiplexer #(.select(1), .width(1), .disabled("Z"), .enable("false")) multiplexer_4 (
    .in0(RegWrite), .in1(1'b0), .out(multiplexer_4_out), .sel(\同步清0_高电平有效 ));
  Multiplexer #(.select(1), .width(1), .disabled("Z"), .enable("false")) multiplexer_5 (
    .in0(RegDst), .in1(1'b0), .out(multiplexer_5_out), .sel(\同步清0_高电平有效 ));
  Multiplexer #(.select(1), .width(1), .disabled("Z"), .enable("false")) multiplexer_6 (
    .in0(JAL), .in1(1'b0), .out(multiplexer_6_out), .sel(\同步清0_高电平有效 ));
  Multiplexer #(.select(1), .width(1), .disabled("Z"), .enable("false")) multiplexer_7 (
    .in0(MemWrite), .in1(1'b0), .out(multiplexer_7_out), .sel(\同步清0_高电平有效 ));
  Multiplexer #(.select(1), .width(1), .disabled("Z"), .enable("false")) multiplexer_8 (
    .in0(SH), .in1(1'b0), .out(multiplexer_8_out), .sel(\同步清0_高电平有效 ));
  Multiplexer #(.select(1), .width(32), .disabled("Z"), .enable("false")) multiplexer_9 (
    .in0(IR), .in1({32{1'b0}}), .out(multiplexer_9_out), .sel(\同步清0_高电平有效 ));
  Multiplexer #(.select(1), .width(32), .disabled("Z"), .enable("false")) multiplexer_10 (
    .in0(PC_4), .in1({32{1'b0}}), .out(multiplexer_10_out), .sel(\同步清0_高电平有效 ));
  Multiplexer #(.select(1), .width(32), .disabled("Z"), .enable("false")) multiplexer_11 (
    .in0(R2), .in1({32{1'b0}}), .out(multiplexer_11_out), .sel(\同步清0_高电平有效 ));
  Multiplexer #(.select(1), .width(32), .disabled("Z"), .enable("false")) multiplexer_12 (
    .in0(Alu), .in1({32{1'b0}}), .out(multiplexer_12_out), .sel(\同步清0_高电平有效 ));
  not not_1 (not_1_out, \使能端_低电平有效 );
  Register #(.width(32), .trigger("rising"), .Select("low")) register_1 (
    .D(multiplexer_1_out), .en(not_1_out), .Q(PC_2), .clk(CLK));  // open: clr
  Register #(.width(32), .trigger("rising"), .Select("low")) register_2 (
    .D(multiplexer_9_out), .en(not_1_out), .Q(IR_2), .clk(CLK));  // open: clr
  Register #(.width(32), .trigger("rising"), .Select("low")) register_3 (
    .D(multiplexer_10_out), .en(not_1_out), .Q(PC_4_2), .clk(CLK));  // open: clr
  Register #(.width(32), .trigger("rising"), .Select("low")) register_4 (
    .D(multiplexer_11_out), .en(not_1_out), .Q(R2_2), .clk(CLK));  // open: clr
  Register #(.width(32), .trigger("rising"), .Select("low")) register_5 (
    .D(multiplexer_12_out), .en(not_1_out), .Q(Alu_2), .clk(CLK));  // open: clr
  Register #(.width(1), .trigger("rising"), .Select("low")) register_6 (
    .D(multiplexer_2_out), .en(not_1_out), .Q(Syscall_2), .clk(CLK));  // open: clr
  Register #(.width(1), .trigger("rising"), .Select("low")) register_7 (
    .D(multiplexer_3_out), .en(not_1_out), .Q(MemToReg_2), .clk(CLK));  // open: clr
  Register #(.width(1), .trigger("rising"), .Select("low")) register_8 (
    .D(multiplexer_4_out), .en(not_1_out), .Q(RegWrite_2), .clk(CLK));  // open: clr
  Register #(.width(1), .trigger("rising"), .Select("low")) register_9 (
    .D(multiplexer_5_out), .en(not_1_out), .Q(RegDst_2), .clk(CLK));  // open: clr
  Register #(.width(1), .trigger("rising"), .Select("low")) register_10 (
    .D(multiplexer_6_out), .en(not_1_out), .Q(JAL_2), .clk(CLK));  // open: clr
  Register #(.width(1), .trigger("rising"), .Select("low")) register_11 (
    .D(multiplexer_7_out), .en(not_1_out), .Q(MemWrite_2), .clk(CLK));  // open: clr
  Register #(.width(1), .trigger("rising"), .Select("low")) register_12 (
    .D(multiplexer_8_out), .en(not_1_out), .Q(SH_2), .clk(CLK));  // open: clr
  Pull_Resistor #(.pull(0)) pull_resistor_1 (.node(\同步清0_高电平有效 ));
  Pull_Resistor #(.pull(0)) pull_resistor_2 (.node(not_1_out));
endmodule

module MEM_WB (
  input  CLK,
  input  \同步清0_高电平有效 ,
  input  \使能端_低电平有效 ,
  input  [31:0] PC,
  input  [31:0] IR,
  input  [31:0] PC_4,
  input  [31:0] MD,
  input  [31:0] Alu,
  input  Syscall,
  input  MemToReg,
  input  RegWrite,
  input  RegDst,
  input  JAL,
  output [31:0] PC_2,
  output [31:0] IR_2,
  output [31:0] PC_4_2,
  output [31:0] MD_2,
  output [31:0] Alu_2,
  output Syscall_2,
  output MemToReg_2,
  output RegWrite_2,
  output RegDst_2,
  output JAL_2
);

  wire multiplexer_2_out, multiplexer_3_out, multiplexer_4_out, multiplexer_5_out, multiplexer_6_out,
       not_1_out;
  wire [31:0] multiplexer_1_out, multiplexer_7_out, multiplexer_8_out, multiplexer_9_out, multiplexer_10_out;

  Multiplexer #(.select(1), .width(32), .disabled("Z"), .enable("false")) multiplexer_1 (
    .in0(PC), .in1({32{1'b0}}), .out(multiplexer_1_out), .sel(\同步清0_高电平有效 ));
  Multiplexer #(.select(1), .width(1), .disabled("Z"), .enable("false")) multiplexer_2 (
    .in0(Syscall), .in1(1'b0), .out(multiplexer_2_out), .sel(\同步清0_高电平有效 ));
  Multiplexer #(.select(1), .width(1), .disabled("Z"), .enable("false")) multiplexer_3 (
    .in0(MemToReg), .in1(1'b0), .out(multiplexer_3_out), .sel(\同步清0_高电平有效 ));
  Multiplexer #(.select(1), .width(1), .disabled("Z"), .enable("false")) multiplexer_4 (
    .in0(RegWrite), .in1(1'b0), .out(multiplexer_4_out), .sel(\同步清0_高电平有效 ));
  Multiplexer #(.select(1), .width(1), .disabled("Z"), .enable("false")) multiplexer_5 (
    .in0(RegDst), .in1(1'b0), .out(multiplexer_5_out), .sel(\同步清0_高电平有效 ));
  Multiplexer #(.select(1), .width(1), .disabled("Z"), .enable("false")) multiplexer_6 (
    .in0(JAL), .in1(1'b0), .out(multiplexer_6_out), .sel(\同步清0_高电平有效 ));
  Multiplexer #(.select(1), .width(32), .disabled("Z"), .enable("false")) multiplexer_7 (
    .in0(IR), .in1({32{1'b0}}), .out(multiplexer_7_out), .sel(\同步清0_高电平有效 ));
  Multiplexer #(.select(1), .width(32), .disabled("Z"), .enable("false")) multiplexer_8 (
    .in0(PC_4), .in1({32{1'b0}}), .out(multiplexer_8_out), .sel(\同步清0_高电平有效 ));
  Multiplexer #(.select(1), .width(32), .disabled("Z"), .enable("false")) multiplexer_9 (
    .in0(MD), .in1({32{1'b0}}), .out(multiplexer_9_out), .sel(\同步清0_高电平有效 ));
  Multiplexer #(.select(1), .width(32), .disabled("Z"), .enable("false")) multiplexer_10 (
    .in0(Alu), .in1({32{1'b0}}), .out(multiplexer_10_out), .sel(\同步清0_高电平有效 ));
  not not_1 (not_1_out, \使能端_低电平有效 );
  Register #(.width(32), .trigger("rising"), .Select("low")) register_1 (
    .D(multiplexer_1_out), .en(not_1_out), .Q(PC_2), .clk(CLK));  // open: clr
  Register #(.width(32), .trigger("rising"), .Select("low")) register_2 (
    .D(multiplexer_7_out), .en(not_1_out), .Q(IR_2), .clk(CLK));  // open: clr
  Register #(.width(32), .trigger("rising"), .Select("low")) register_3 (
    .D(multiplexer_8_out), .en(not_1_out), .Q(PC_4_2), .clk(CLK));  // open: clr
  Register #(.width(32), .trigger("rising"), .Select("low")) register_4 (
    .D(multiplexer_9_out), .en(not_1_out), .Q(MD_2), .clk(CLK));  // open: clr
  Register #(.width(32), .trigger("rising"), .Select("low")) register_5 (
    .D(multiplexer_10_out), .en(not_1_out), .Q(Alu_2), .clk(CLK));  // open: clr
  Register #(.width(1), .trigger("rising"), .Select("low")) register_6 (
    .D(multiplexer_2_out), .en(not_1_out), .Q(Syscall_2), .clk(CLK));  // open: clr
  Register #(.width(1), .trigger("rising"), .Select("low")) register_7 (
    .D(multiplexer_3_out), .en(not_1_out), .Q(MemToReg_2), .clk(CLK));  // open: clr
  Register #(.width(1), .trigger("rising"), .Select("low")) register_8 (
    .D(multiplexer_4_out), .en(not_1_out), .Q(RegWrite_2), .clk(CLK));  // open: clr
  Register #(.width(1), .trigger("rising"), .Select("low")) register_9 (
    .D(multiplexer_5_out), .en(not_1_out), .Q(RegDst_2), .clk(CLK));  // open: clr
  Register #(.width(1), .trigger("rising"), .Select("low")) register_10 (
    .D(multiplexer_6_out), .en(not_1_out), .Q(JAL_2), .clk(CLK));  // open: clr
  Pull_Resistor #(.pull(0)) pull_resistor_1 (.node(\同步清0_高电平有效 ));
  Pull_Resistor #(.pull(0)) pull_resistor_2 (.node(not_1_out));
endmodule

module \数据冲突检测  (
  input  RsUsed,
  input  RtUsed,
  input  [4:0] rs,
  input  [4:0] rt,
  input  EX_RegWrite,
  input  MEM_RegWrite,
  input  [4:0] EX_WriteReg_num,
  input  [4:0] MEM_WriteReg_num,
  input  EX_MemToReg,
  output R1_EX_DaraHazarrd,
  output R2_EX_DaraHazarrd,
  output DataHazzard,
  output R1_MEM_DaraHazarrd,
  output R2_MEM_DaraHazarrd,
  output LoadUse
);

  wire comparator_1_eq, comparator_2_eq, comparator_3_eq, comparator_4_eq, comparator_5_eq, comparator_6_eq,
       not_1_out, not_2_out, or_1_out;

  Comparator #(.width(5), .mode("twosComplement")) comparator_1 (
    .a(rs), .b({5{1'b0}}), .eq(comparator_1_eq));  // open: gt, lt
  not not_1 (not_1_out, comparator_1_eq);
  Comparator #(.width(5), .mode("twosComplement")) comparator_2 (
    .a(rt), .b({5{1'b0}}), .eq(comparator_2_eq));  // open: gt, lt
  not not_2 (not_2_out, comparator_2_eq);
  Comparator #(.width(5), .mode("twosComplement")) comparator_3 (
    .a(EX_WriteReg_num), .b(rs), .eq(comparator_3_eq));  // open: gt, lt
  Comparator #(.width(5), .mode("twosComplement")) comparator_4 (
    .a(EX_WriteReg_num), .b(rt), .eq(comparator_4_eq));  // open: gt, lt
  Comparator #(.width(5), .mode("twosComplement")) comparator_5 (
    .a(MEM_WriteReg_num), .b(rs), .eq(comparator_5_eq));  // open: gt, lt
  Comparator #(.width(5), .mode("twosComplement")) comparator_6 (
    .a(MEM_WriteReg_num), .b(rt), .eq(comparator_6_eq));  // open: gt, lt
  and and_1 (R1_EX_DaraHazarrd, RsUsed, not_1_out, EX_RegWrite, comparator_3_eq);
  and and_2 (R2_EX_DaraHazarrd, RtUsed, not_2_out, EX_RegWrite, comparator_4_eq);
  and and_3 (R1_MEM_DaraHazarrd, RsUsed, not_1_out, MEM_RegWrite, comparator_5_eq);
  and and_4 (R2_MEM_DaraHazarrd, RtUsed, not_2_out, MEM_RegWrite, comparator_6_eq);
  or or_1 (or_1_out, R2_EX_DaraHazarrd, R1_EX_DaraHazarrd);
  and and_5 (LoadUse, or_1_out, EX_MemToReg);
  or or_2 (DataHazzard, R1_EX_DaraHazarrd, R2_EX_DaraHazarrd, R1_MEM_DaraHazarrd, R2_MEM_DaraHazarrd);
endmodule
